// Logisim project Claire_W_Lab1_VendingMachine.circ as structural Verilog: 1 circuit, main circuit main
module main (
  input  Q,
  input  D1,
  input  D2,
  input  D3,
  output Vend,
  output Change1,
  output Change2,
  output Change3
);

  wire and_1_out, and_2_out, and_3_out, and_4_out, and_5_out, and_6_out, and_7_out, and_8_out, and_9_out,
       and_10_out, and_11_out, and_12_out, and_13_out, and_14_out, not_1_out, not_2_out, not_3_out,
       not_4_out, or_1_out, or_2_out, or_3_out, or_4_out;

  not not_1 (not_1_out, Q);
  not not_2 (not_2_out, D1);
  not not_3 (not_3_out, D2);
  not not_4 (not_4_out, D3);
  and and_1 (and_1_out, not_2_out, not_3_out, D3);
  and and_2 (and_2_out, D2, not_2_out, not_4_out);
  and and_3 (and_3_out, D1, not_3_out, not_4_out);
  or or_1 (or_1_out, and_1_out, and_2_out, and_3_out);
  and and_4 (and_4_out, D1, D2, D3);
  and and_5 (and_5_out, not_2_out, not_3_out, not_4_out);
  and and_6 (and_6_out, D1, D2, not_4_out);
  and and_7 (and_7_out, D1, not_3_out, D3);
  and and_8 (and_8_out, not_2_out, D2, D3);
  or or_2 (or_2_out, D1, D2, D3);
  or or_3 (or_3_out, and_4_out, and_5_out);
  or or_4 (or_4_out, and_6_out, and_7_out, and_8_out);
  and and_9 (and_9_out, Q, or_2_out);
  and and_10 (and_10_out, not_1_out, D1, D2, D3);
  and and_11 (and_11_out, Q, or_3_out);
  and and_12 (and_12_out, not_1_out, or_4_out);
  and and_13 (and_13_out, Q, or_4_out);
  and and_14 (and_14_out, not_1_out, or_1_out);
  or or_5 (Vend, and_9_out, and_10_out);
  or or_6 (Change1, and_11_out, and_12_out);
  or or_7 (Change2, and_13_out, and_14_out);

  assign Change3 = Q;
endmodule
