// Logisim project LAB4.circ as structural Verilog: 1 circuit, main circuit main
module main (
  input  [3:0] Load_data,
  input  Load,
  input  Shift,
  input  In,
  input  Clear,
  input  Load_2,
  input  [1:0] Load_In_2__3,
  input  [1:0] Load_In_0__1,
  input  Count,
  input  Clear_2,
  input  [2:0] Address,
  output Out,
  output [3:0] Data_Out,
  output [3:0] Data_Out_2,
  output [7:0] out_15
);

  wire and_1_out, clock_1_out, clock_2_out, shift_register_1_out;

  Shift_Register #(.length(2)) shift_register_1 (
    .shift(Shift), .in(In), .clk(clock_1_out), .out(shift_register_1_out), .load(Load), .clr(Clear),
    .d0(Load_data[3]), .q0(Data_Out[3]), .d1(Load_data[2]), .q1(Data_Out[2]));
  Clock clock_1 (.out(clock_1_out));
  Clock clock_2 (.out(clock_2_out));
  Shift_Register #(.length(2)) shift_register_2 (
    .shift(Shift), .in(shift_register_1_out), .clk(clock_1_out), .out(Out), .load(Load), .clr(Clear),
    .d0(Load_data[1]), .q0(Data_Out[1]), .d1(Load_data[0]), .q1(Data_Out[0]));
  Counter #(.width(2), .max('h3)) counter_1 (
    .load(Load_2), .D(Load_In_0__1), .count(Count), .Q(Data_Out_2[1:0]), .clk(clock_2_out), .clr(Clear_2));  // open: carry
  Multiplexer #(.select(3), .width(8), .enable("false")) multiplexer_1 (
    .in0(8'h12), .in1(8'h44), .in2(8'h7), .in3({8{1'b1}}), .in4({8{1'b0}}), .in5(8'h23), .in6(8'h12),
    .in7(8'h22), .out(out_15), .sel(Address));
  Counter #(.width(2), .max('h3)) counter_2 (
    .load(Load_2), .D(Load_In_2__3), .count(Count), .Q(Data_Out_2[3:2]), .clk(and_1_out), .clr(Clear_2));  // open: carry
  and and_1 (and_1_out, ~Data_Out_2[0], ~Data_Out_2[1]);  // AND_Gate
endmodule
