// Logisim project LAB6.circ as structural Verilog: 25 circuits, main circuit main
module main (
  input  [3:0] Op,
  input  cb,
  input  [3:0] c_v_z_s,
  input  Rd_Ra_Sel,
  input  F_Sel,
  input  LO_HI_Sel,
  input  SET_sel,
  input  RAM_wr_en,
  input  L_S_F_sel,
  input  SETF_CLRF_en,
  input  memory_sel,
  input  Reg_en,
  input  R13_en,
  input  clear,
  output [3:0] out_15
);

  wire clock_out, multiplexer_5_out, multiplexer_6_out;
  wire [3:0] multiplexer_1_out, multiplexer_7_out, rom_1_data, rom_1_data_2, rom_1_data_3;
  wire [4:0] alsu_1_flag_out, flag_module_1_sign_out;
  wire [15:0] alsu_1_data_d, alsu_1_r13_rt, counter_1_q, Expansion_Module_out_2, multiplexer_2_out,
       multiplexer_3_out, multiplexer_4_out, ram_1_data, register_file_1_data_a, register_file_1_data_b,
       sign_extension_1_out_3;

  Clock clock (.out(clock_out));
  Counter #(.width(16), .max('hffff)) counter_1 (
    .count(1'b1), .Q(counter_1_q), .clk(clock_out), .clr(clear));  // open: load, D, carry
  Hex_Digit_Display hex_digit_display_1 (.value(rom_1_data));  // open: dp
  Hex_Digit_Display hex_digit_display_2 (.value(rom_1_data_2));  // open: dp
  Hex_Digit_Display hex_digit_display_3 (.value(out_15));  // open: dp
  Hex_Digit_Display hex_digit_display_4 (.value(rom_1_data_3));  // open: dp
  ROM #(.addrWidth(16), .dataWidth(16)) rom_1 (
    .addr(counter_1_q), .data({rom_1_data_2, rom_1_data, out_15, rom_1_data_3}));  // open: sel
  Control_Unit Control_Unit (.Op_Code(rom_1_data_2));
  Expansion_Module Expansion_Module (.in_1(out_15), .out_2(Expansion_Module_out_2));
  Multiplexer #(.width(4), .enable("false")) multiplexer_1 (
    .in0(rom_1_data), .in1(out_15), .out(multiplexer_1_out), .sel(Rd_Ra_Sel));
  Register_File register_file_1 (
    .Data_In(multiplexer_4_out), .write_enable(Reg_en), .destination_addr(rom_1_data), .clear(clear),
    .regB_addr(rom_1_data_3), .regA_addr(multiplexer_1_out), .Data_a(register_file_1_data_a),
    .Data_b(register_file_1_data_b), .clock(clock_out), .R13(alsu_1_r13_rt), .R13_en(R13_en));
  sign_extension sign_extension_1 (.out_3(sign_extension_1_out_3), .in_2({out_15, rom_1_data_3}), .in_1(LO_HI_Sel));
  Multiplexer #(.width(16), .enable("false")) multiplexer_2 (
    .in0(Expansion_Module_out_2), .in1(register_file_1_data_a), .out(multiplexer_2_out), .sel(F_Sel));
  Multiplexer #(.width(16), .enable("false")) multiplexer_3 (
    .in0(register_file_1_data_b), .in1(sign_extension_1_out_3), .out(multiplexer_3_out), .sel(SET_sel));
  Multiplexer #(.width(16), .enable("false")) multiplexer_4 (
    .in0(alsu_1_data_d), .in1(ram_1_data), .out(multiplexer_4_out), .sel(memory_sel));
  ALSU alsu_1 (
    .flag_in(flag_module_1_sign_out), .Data_a(multiplexer_2_out), .Data_b(multiplexer_3_out),
    .flag_out(alsu_1_flag_out), .Data_d(alsu_1_data_d), .op(Op), .R13_Rt(alsu_1_r13_rt));
  Multiplexer #(.enable("false")) multiplexer_5 (
    .in0(rom_1_data_2[1]), .in1(alsu_1_flag_out[0]), .out(multiplexer_5_out), .sel(L_S_F_sel));
  Multiplexer #(.enable("false")) multiplexer_6 (
    .in0(cb), .in1(out_15[0]), .out(multiplexer_6_out), .sel(SETF_CLRF_en));
  Multiplexer #(.width(4), .enable("false")) multiplexer_7 (
    .in0(c_v_z_s), .in1(rom_1_data_3), .out(multiplexer_7_out), .sel(SETF_CLRF_en));
  Flag_Module flag_module_1 (
    .sign_out(flag_module_1_sign_out[0]), .zero_out(flag_module_1_sign_out[1]),
    .overflow_out(flag_module_1_sign_out[2]), .carry_out(flag_module_1_sign_out[3]),
    .carry_block_out(flag_module_1_sign_out[4]), .sign_in(multiplexer_5_out), .zero_in(alsu_1_flag_out[1]),
    .overflow_in(alsu_1_flag_out[2]), .carry_in(alsu_1_flag_out[3]), .carry_block_in(alsu_1_flag_out[4]),
    .Write_in_0(multiplexer_7_out[0]), .Write_in_1(multiplexer_7_out[1]), .Write_in_2(multiplexer_7_out[2]),
    .Write_in_3(multiplexer_7_out[3]), .Write_in_4(multiplexer_6_out));
  LED sign (.in(flag_module_1_sign_out[0]));
  LED zero (.in(flag_module_1_sign_out[1]));
  LED overflow (.in(flag_module_1_sign_out[2]));
  LED carry (.in(flag_module_1_sign_out[3]));
  LED carry_block (.in(flag_module_1_sign_out[4]));
  RAM #(.addrWidth(16), .dataWidth(16), .bus("separate")) ram_1 (
    .addr(alsu_1_data_d), .din(register_file_1_data_a), .data(ram_1_data), .str(RAM_wr_en), .sel(1'b0),
    .clk(clock_out), .ld(1'b1), .clr(1'b0));

  // Notes on the sheet:
  //   Instruction ROM
  //   contents of rom_1 (hex, n*v repeats v):
  //   e10a f100 e31e f300 a111 a213
  //   RAM
endmodule

// Reigister File
module Register_File (
  input  [15:0] Data_In,
  input  write_enable,
  input  [3:0] destination_addr,
  input  [15:0] R13,
  input  R13_en,
  input  clear,
  input  clock,
  input  [3:0] regB_addr,
  input  [3:0] regA_addr,
  output [15:0] Data_a,
  output [15:0] Data_b
);

  wire decoder_1_out0, decoder_1_out1, decoder_1_out2, decoder_1_out3, decoder_1_out4, decoder_1_out5,
       decoder_1_out6, decoder_1_out7, decoder_1_out8, decoder_1_out9, decoder_1_out10, decoder_1_out11,
       decoder_1_out12, decoder_1_out14, decoder_1_out15;
  wire [15:0] multiplexer_1_out, R0_q, R1_q, R2_q, R3_q, R4_q, R5_q, R6_q, R7_q, R8_q, R9_q, R10_q, R11_q,
       R12_q, R13_q, R14_q, R15_q;

  Decoder #(.select(4), .disabled(0)) decoder_1 (
    .out0(decoder_1_out0), .out1(decoder_1_out1), .out2(decoder_1_out2), .out3(decoder_1_out3),
    .out4(decoder_1_out4), .out5(decoder_1_out5), .out6(decoder_1_out6), .out7(decoder_1_out7),
    .out8(decoder_1_out8), .out9(decoder_1_out9), .out10(decoder_1_out10), .out11(decoder_1_out11),
    .out12(decoder_1_out12), .out13(clock), .out14(decoder_1_out14), .out15(decoder_1_out15),
    .sel(destination_addr), .en(write_enable));
  Register #(.width(16)) R0 (.D({16{1'b0}}), .en(decoder_1_out0), .Q(R0_q), .clk(clock), .clr(clear));
  Register #(.width(16)) R2 (.D(Data_In), .en(decoder_1_out2), .Q(R2_q), .clk(clock), .clr(clear));
  Register #(.width(16)) R4 (.D(Data_In), .en(decoder_1_out4), .Q(R4_q), .clk(clock), .clr(clear));
  Register #(.width(16)) R6 (.D(Data_In), .en(decoder_1_out6), .Q(R6_q), .clk(clock), .clr(clear));
  Register #(.width(16)) R8 (.D(Data_In), .en(decoder_1_out8), .Q(R8_q), .clk(clock), .clr(clear));
  Register #(.width(16)) R10 (.D(Data_In), .en(decoder_1_out10), .Q(R10_q), .clk(clock), .clr(clear));
  Register #(.width(16)) R12 (.D(Data_In), .en(decoder_1_out12), .Q(R12_q), .clk(clock), .clr(clear));
  Register #(.width(16)) R14 (.D(Data_In), .en(decoder_1_out14), .Q(R14_q), .clk(clock), .clr(clear));
  Multiplexer #(.width(16), .enable("false")) multiplexer_1 (
    .in0(Data_In), .in1(R13), .out(multiplexer_1_out), .sel(R13_en));
  Register #(.width(16)) R1 (.D(Data_In), .en(decoder_1_out1), .Q(R1_q), .clk(clock), .clr(clear));
  Register #(.width(16)) R3 (.D(Data_In), .en(decoder_1_out3), .Q(R3_q), .clk(clock), .clr(clear));
  Register #(.width(16)) R5 (.D(Data_In), .en(decoder_1_out5), .Q(R5_q), .clk(clock), .clr(clear));
  Register #(.width(16)) R7 (.D(Data_In), .en(decoder_1_out7), .Q(R7_q), .clk(clock), .clr(clear));
  Register #(.width(16)) R9 (.D(Data_In), .en(decoder_1_out9), .Q(R9_q), .clk(clock), .clr(clear));
  Register #(.width(16)) R11 (.D(Data_In), .en(decoder_1_out11), .Q(R11_q), .clk(clock), .clr(clear));
  Register #(.width(16)) u_R13 (.D(multiplexer_1_out), .en(clock), .Q(R13_q), .clk(clock), .clr(clear));
  Register #(.width(16)) R15 (.D(Data_In), .en(decoder_1_out15), .Q(R15_q), .clk(clock), .clr(clear));
  Multiplexer #(.select(4), .width(16), .enable("false")) multiplexer_2 (
    .in0(R0_q), .in1(R1_q), .in2(R2_q), .in3(R3_q), .in4(R4_q), .in5(R5_q), .in6(R6_q), .in7(R7_q),
    .in8(R8_q), .in9(R9_q), .in10(R10_q), .in11(R11_q), .in12(R12_q), .in13(R13_q), .in14(R14_q),
    .in15(R15_q), .out(Data_a), .sel(regA_addr));
  Multiplexer #(.select(4), .width(16), .enable("false")) multiplexer_3 (
    .in0(R0_q), .in1(R1_q), .in2(R2_q), .in3(R3_q), .in4(R4_q), .in5(R5_q), .in6(R6_q), .in7(R7_q),
    .in8(R8_q), .in9(R9_q), .in10(R10_q), .in11(R11_q), .in12(R12_q), .in13(R13_q), .in14(R14_q),
    .in15(R15_q), .out(Data_b), .sel(regB_addr));

  // Notes on the sheet:
  //   sixteen 16-bit Register file
endmodule

module ALSU (
  input  [4:0] flag_in,
  input  [3:0] op,
  input  [15:0] Data_a,
  input  [15:0] Data_b,
  output [4:0] flag_out,
  output [15:0] Data_d,
  output [15:0] R13_Rt
);

  wire [4:0] add_1_flag_out, and_1_flag_out, dec_1_flag_out, inc_1_flag_out, lsl_1_flag_out, lsr_1_flag_out,
       mult_1_flag_out, or_1_flag_out, rstrf_1_flag_out, savf_1_flag_out, setf_clrf_1_flag_out,
       setlo_hi_1_flag_out, sub_1_flag_out, xor_1_flag_out;
  wire [15:0] add_1_data_d, and_1_out, dec_1_data_d, inc_1_data_d, lsl_1_data_d, lsr_1_data_d, mult_1_result,
       or_1_out, rstrf_1_data_d, savf_1_data_d, setf_clrf_1_data_d, setlo_hi_1_data_d, sub_1_data_d,
       xor_1_data_d;

  SETLO_HI setlo_hi_1 (
    .flag_in(flag_in), .Data_a(Data_a), .Data_b(Data_b), .flag_out(setlo_hi_1_flag_out),
    .Data_d(setlo_hi_1_data_d));
  AND and_1 (.flag_in(flag_in), .Data_a(Data_a), .Data_b(Data_b), .flag_out(and_1_flag_out), .out(and_1_out));
  OR or_1 (.flag_in(flag_in), .Data_a(Data_a), .Data_b(Data_b), .flag_out(or_1_flag_out), .out(or_1_out));
  ADD add_1 (.flag_in(flag_in), .Data_a(Data_a), .Data_b(Data_b), .flag_out(add_1_flag_out), .Data_d(add_1_data_d));
  SUB sub_1 (.flag_in(flag_in), .Data_a(Data_a), .Data_b(Data_b), .flag_out(sub_1_flag_out), .Data_d(sub_1_data_d));
  MULT mult_1 (
    .flag_in(flag_in), .Data_a(Data_a), .Data_b(Data_b), .flag_out(mult_1_flag_out), .Result(mult_1_result),
    .Overflow(R13_Rt));
  XOR xor_1 (.flag_in(flag_in), .Data_a(Data_a), .Data_b(Data_b), .flag_out(xor_1_flag_out), .Data_d(xor_1_data_d));
  LSL lsl_1 (.flag_in(flag_in), .Data_a(Data_a), .Data_b(Data_b), .flag_out(lsl_1_flag_out), .Data_d(lsl_1_data_d));
  LSR lsr_1 (.flag_in(flag_in), .Data_a(Data_a), .Data_b(Data_b), .flag_out(lsr_1_flag_out), .Data_d(lsr_1_data_d));
  SETF_CLRF setf_clrf_1 (
    .flag_in(flag_in), .Data_a(Data_a), .Data_b(Data_b), .flag_out(setf_clrf_1_flag_out),
    .Data_d(setf_clrf_1_data_d));
  SAVF savf_1 (.flag_in(flag_in), .Data_a(Data_a), .Data_b(Data_b), .flag_out(savf_1_flag_out), .Data_d(savf_1_data_d));
  RSTRF rstrf_1 (
    .flag_in(flag_in), .Data_a(Data_a), .Data_b(Data_b), .flag_out(rstrf_1_flag_out), .Data_d(rstrf_1_data_d));
  INC inc_1 (.flag_in(flag_in), .Data_a(Data_a), .Data_b(Data_b), .flag_out(inc_1_flag_out), .Data_d(inc_1_data_d));
  DEC dec_1 (.flag_in(flag_in), .Data_a(Data_a), .Data_b(Data_b), .flag_out(dec_1_flag_out), .Data_d(dec_1_data_d));
  MUX mux_1 (
    .flag0(setlo_hi_1_flag_out), .In0(setlo_hi_1_data_d), .flag1(and_1_flag_out), .In1(and_1_out),
    .flag2(or_1_flag_out), .In2(or_1_out), .flag3(add_1_flag_out), .In3(add_1_data_d),
    .flag4(sub_1_flag_out), .In4(sub_1_data_d), .flag5(mult_1_flag_out), .In5(mult_1_result),
    .flag6(xor_1_flag_out), .In6(xor_1_data_d), .flag7(lsl_1_flag_out), .In7(lsl_1_data_d),
    .flag8(lsr_1_flag_out), .In8(lsr_1_data_d), .flag9(setf_clrf_1_flag_out), .In9(setf_clrf_1_data_d),
    .flag10(savf_1_flag_out), .In10(savf_1_data_d), .flag11(rstrf_1_flag_out), .In11(rstrf_1_data_d),
    .flag12(inc_1_flag_out), .In12(inc_1_data_d), .flag13(dec_1_flag_out), .In13(dec_1_data_d),
    .flag_out(flag_out), .\output (Data_d), .op(op));  // open: flag14, In14, flag15, In15
endmodule

module SETLO_HI (
  input  [4:0] flag_in,
  input  [15:0] Data_a,
  input  [15:0] Data_b,
  output [4:0] flag_out,
  output [15:0] Data_d
);

  wire flags_in_1_carry_block_in, flags_in_1_carry_in, flags_in_1_overflow_in, flags_in_1_sign_in,
       flags_in_1_zero_in;

  Flags_in flags_in_1 (
    .flag_in(flag_in), .Sign_in(flags_in_1_sign_in), .Zero_in(flags_in_1_zero_in),
    .Overflow_in(flags_in_1_overflow_in), .Carry_in(flags_in_1_carry_in),
    .Carry_block_in(flags_in_1_carry_block_in));
  Flags_out flags_out_1 (
    .Sign_out(flags_in_1_sign_in), .Zero_out(flags_in_1_zero_in), .Overflow_out(flags_in_1_overflow_in),
    .Carry_out(flags_in_1_carry_in), .Carry_block_out(flags_in_1_carry_block_in), .flag_out(flag_out));

  assign Data_d = Data_b;
endmodule

module ADD (
  input  [4:0] flag_in,
  input  [15:0] Data_a,
  input  [15:0] Data_b,
  output [4:0] flag_out,
  output [15:0] Data_d
);

  wire Adder_carry_out, Adder_overflow, and_1_out, comparator_1_eq, comparator_1_lt, Flags_in_carry_block_in,
       Flags_in_carry_in, not_1_out;

  Flags_in Flags_in (
    .flag_in(flag_in), .Carry_in(Flags_in_carry_in), .Carry_block_in(Flags_in_carry_block_in));  // open: Sign_in, Zero_in, Overflow_in
  and and_1 (and_1_out, Flags_in_carry_in, not_1_out);
  not not_1 (not_1_out, Flags_in_carry_block_in);
  Adder_Subtractor Adder (
    .a(Data_a), .b(Data_b), .Adder_Subtractor_Select(1'b0), .Carry_in(and_1_out),
    .Carry_out(Adder_carry_out), .Output(Data_d), .Overflow(Adder_overflow));
  Comparator #(.width(16)) comparator_1 (
    .a({16{1'b0}}), .b(Data_d), .eq(comparator_1_eq), .lt(comparator_1_lt));  // open: gt
  Flags_out Flags_out (
    .Sign_out(comparator_1_lt), .Zero_out(comparator_1_eq), .Overflow_out(Adder_overflow),
    .Carry_out(Adder_carry_out), .Carry_block_out(Flags_in_carry_block_in), .flag_out(flag_out));
endmodule

module MUX (
  input  [3:0] op,
  input  [4:0] flag0,
  input  [15:0] In0,
  input  [4:0] flag1,
  input  [15:0] In1,
  input  [4:0] flag2,
  input  [15:0] In2,
  input  [4:0] flag3,
  input  [15:0] In3,
  input  [4:0] flag4,
  input  [15:0] In4,
  input  [4:0] flag5,
  input  [15:0] In5,
  input  [4:0] flag6,
  input  [15:0] In6,
  input  [4:0] flag7,
  input  [15:0] In7,
  input  [4:0] flag8,
  input  [15:0] In8,
  input  [4:0] flag9,
  input  [15:0] In9,
  input  [4:0] flag10,
  input  [15:0] In10,
  input  [4:0] flag11,
  input  [15:0] In11,
  input  [4:0] flag12,
  input  [15:0] In12,
  input  [4:0] flag13,
  input  [15:0] In13,
  input  [4:0] flag14,
  input  [15:0] In14,
  input  [4:0] flag15,
  input  [15:0] In15,
  output [4:0] flag_out,
  output [15:0] \output 
);

  Multiplexer #(.select(4), .width(5), .enable("false")) multiplexer_1 (
    .in0(flag0), .in1(flag1), .in2(flag2), .in3(flag3), .in4(flag4), .in5(flag5), .in6(flag6), .in7(flag7),
    .in8(flag8), .in9(flag9), .in10(flag10), .in11(flag11), .in12(flag12), .in13(flag13), .in14(flag14),
    .in15(flag15), .out(flag_out), .sel(op));
  Multiplexer #(.select(4), .width(16), .enable("false")) multiplexer_2 (
    .in0(In0), .in1(In1), .in2(In2), .in3(In3), .in4(In4), .in5(In5), .in6(In6), .in7(In7), .in8(In8),
    .in9(In9), .in10(In10), .in11(In11), .in12(In12), .in13(In13), .in14(In14), .in15(In15), .out(\output ),
    .sel(op));
endmodule

module AND (
  input  [4:0] flag_in,
  input  [15:0] Data_a,
  input  [15:0] Data_b,
  output [4:0] flag_out,
  output [15:0] out
);

  wire comparator_1_eq, comparator_1_lt, flags_in_1_carry_block_in, flags_in_1_carry_in,
       flags_in_1_overflow_in;

  Flags_in flags_in_1 (
    .flag_in(flag_in), .Overflow_in(flags_in_1_overflow_in), .Carry_in(flags_in_1_carry_in),
    .Carry_block_in(flags_in_1_carry_block_in));  // open: Sign_in, Zero_in
  assign out = Data_a & Data_b;  // AND_Gate and_1, 16 bits wide
  Comparator #(.width(16)) comparator_1 (
    .a({16{1'b0}}), .b(out), .eq(comparator_1_eq), .lt(comparator_1_lt));  // open: gt
  Flags_out Flags_out (
    .Sign_out(comparator_1_lt), .Zero_out(comparator_1_eq), .Overflow_out(flags_in_1_overflow_in),
    .Carry_out(flags_in_1_carry_in), .Carry_block_out(flags_in_1_carry_block_in), .flag_out(flag_out));
endmodule

module Flag_Module (
  input  sign_in,
  input  zero_in,
  input  overflow_in,
  input  carry_in,
  input  carry_block_in,
  input  Write_in_0,
  input  Write_in_1,
  input  Write_in_2,
  input  Write_in_3,
  input  Write_in_4,
  output sign_out,
  output zero_out,
  output overflow_out,
  output carry_out,
  output carry_block_out
);

  wire clock_out;

  Clock clock (.out(clock_out));
  D_Flip_Flop F0 (
    .clk(clock_out), .D(sign_in), .Q(sign_out), .preset(1'b0), .en(Write_in_0), .reset(1'b0));  // open: Qn
  D_Flip_Flop F1 (
    .clk(clock_out), .D(zero_in), .Q(zero_out), .preset(1'b0), .en(Write_in_1), .reset(1'b0));  // open: Qn
  D_Flip_Flop F2 (
    .clk(clock_out), .D(overflow_in), .Q(overflow_out), .preset(1'b0), .en(Write_in_2), .reset(1'b0));  // open: Qn
  D_Flip_Flop F3 (
    .clk(clock_out), .D(carry_in), .Q(carry_out), .preset(1'b0), .en(Write_in_4), .reset(1'b0));  // open: Qn
  D_Flip_Flop F4 (
    .clk(clock_out), .D(carry_block_in), .Q(carry_block_out), .preset(1'b0), .en(Write_in_3), .reset(1'b0));  // open: Qn
endmodule

module SUB (
  input  [4:0] flag_in,
  input  [15:0] Data_a,
  input  [15:0] Data_b,
  output [4:0] flag_out,
  output [15:0] Data_d
);

  wire and_1_out, comparator_1_eq, comparator_1_lt, Flags_in_carry_block_in, Flags_in_carry_in, not_1_out,
       Sub_carry_out, Sub_overflow;

  Flags_in Flags_in (
    .flag_in(flag_in), .Carry_in(Flags_in_carry_in), .Carry_block_in(Flags_in_carry_block_in));  // open: Sign_in, Zero_in, Overflow_in
  not not_1 (not_1_out, Flags_in_carry_block_in);
  and and_1 (and_1_out, Flags_in_carry_in, not_1_out);
  Adder_Subtractor Sub (
    .a(Data_a), .b(Data_b), .Adder_Subtractor_Select(1'b1), .Carry_in(and_1_out), .Carry_out(Sub_carry_out),
    .Output(Data_d), .Overflow(Sub_overflow));
  Comparator #(.width(16)) comparator_1 (
    .a({16{1'b0}}), .b(Data_d), .eq(comparator_1_eq), .lt(comparator_1_lt));  // open: gt
  Flags_out Flags_out (
    .Sign_out(comparator_1_lt), .Zero_out(comparator_1_eq), .Overflow_out(Sub_overflow),
    .Carry_out(Sub_carry_out), .Carry_block_out(Flags_in_carry_block_in), .flag_out(flag_out));
endmodule

module LSL (
  input  [4:0] flag_in,
  input  [15:0] Data_a,
  input  [15:0] Data_b,
  output [4:0] flag_out,
  output [15:0] Data_d
);

  wire Flags_in_carry_block_in, Flags_in_carry_in, Flags_in_sign_in, Flags_in_zero_in, not_1_out, xor_1_out;

  Flags_in Flags_in (
    .flag_in(flag_in), .Sign_in(Flags_in_sign_in), .Zero_in(Flags_in_zero_in), .Carry_in(Flags_in_carry_in),
    .Carry_block_in(Flags_in_carry_block_in));  // open: Overflow_in
  not not_1 (not_1_out, Flags_in_carry_in);
  and and_1 (Data_d[0], not_1_out, Flags_in_carry_block_in);
  xor xor_1 (xor_1_out, Data_b[14], Data_b[15]);
  Flags_out flags_out (
    .Sign_out(Flags_in_sign_in), .Zero_out(Flags_in_zero_in), .Overflow_out(xor_1_out),
    .Carry_out(Data_b[15]), .Carry_block_out(Flags_in_carry_block_in), .flag_out(flag_out));

  assign Data_d[15:1] = Data_b[14:0];
endmodule

module LSR (
  input  [4:0] flag_in,
  input  [15:0] Data_a,
  input  [15:0] Data_b,
  output [4:0] flag_out,
  output [15:0] Data_d
);

  wire Flags_in_carry_block_in, Flags_in_carry_in, Flags_in_overflow_in, Flags_in_sign_in, Flags_in_zero_in,
       not_1_out;

  Flags_in Flags_in (
    .flag_in(flag_in), .Sign_in(Flags_in_sign_in), .Zero_in(Flags_in_zero_in),
    .Overflow_in(Flags_in_overflow_in), .Carry_in(Flags_in_carry_in), .Carry_block_in(Flags_in_carry_block_in));
  not not_1 (not_1_out, Flags_in_carry_in);
  and and_1 (Data_d[15], not_1_out, Flags_in_carry_block_in);
  Flags_out flags_out (
    .Sign_out(Flags_in_sign_in), .Zero_out(Flags_in_zero_in), .Overflow_out(Flags_in_overflow_in),
    .Carry_out(Data_b[0]), .Carry_block_out(Flags_in_carry_block_in), .flag_out(flag_out));

  assign Data_d[14:0] = Data_b[15:1];
endmodule

module SETF_CLRF (
  input  [4:0] flag_in,
  input  [15:0] Data_a,
  input  [15:0] Data_b,
  output [4:0] flag_out,
  output [15:0] Data_d
);

  Flags_in flags_in_1 (.flag_in(flag_in));  // open: Sign_in, Zero_in, Overflow_in, Carry_in, Carry_block_in
  Flags_out flags_out_1 (
    .Sign_out(Data_a[3]), .Zero_out(Data_a[3]), .Overflow_out(Data_a[3]), .Carry_out(Data_a[3]),
    .Carry_block_out(Data_a[3]), .flag_out(flag_out));

  assign Data_d = {16{1'b0}};
endmodule

module XOR (
  input  [4:0] flag_in,
  input  [15:0] Data_a,
  input  [15:0] Data_b,
  output [4:0] flag_out,
  output [15:0] Data_d
);

  wire comparator_1_eq, comparator_1_lt, flags_in_1_carry_block_in, flags_in_1_carry_in,
       flags_in_1_overflow_in;

  Flags_in flags_in_1 (
    .flag_in(flag_in), .Overflow_in(flags_in_1_overflow_in), .Carry_in(flags_in_1_carry_in),
    .Carry_block_in(flags_in_1_carry_block_in));  // open: Sign_in, Zero_in
  assign Data_d = Data_a ^ Data_b;  // XOR_Gate xor_1, 16 bits wide
  Comparator #(.width(16)) comparator_1 (
    .a({16{1'b0}}), .b(Data_d), .eq(comparator_1_eq), .lt(comparator_1_lt));  // open: gt
  Flags_out Flags_out (
    .Sign_out(comparator_1_lt), .Zero_out(comparator_1_eq), .Overflow_out(flags_in_1_overflow_in),
    .Carry_out(flags_in_1_carry_in), .Carry_block_out(flags_in_1_carry_block_in), .flag_out(flag_out));
endmodule

module MULT (
  input  [4:0] flag_in,
  input  [15:0] Data_a,
  input  [15:0] Data_b,
  output [4:0] flag_out,
  output [15:0] Result,
  output [15:0] Overflow
);

  wire comparator_1_eq, comparator_1_lt, comparator_2_eq, flags_in_1_carry_block_in, flags_in_1_carry_in,
       not_1_out;

  Flags_in flags_in_1 (
    .flag_in(flag_in), .Carry_in(flags_in_1_carry_in), .Carry_block_in(flags_in_1_carry_block_in));  // open: Sign_in, Zero_in, Overflow_in
  Multiplier #(.width(16)) multiplier_1 (.a(Data_a), .b(Data_b), .out(Result), .cout(Overflow));  // open: cin
  Comparator #(.width(16)) comparator_1 (
    .a({16{1'b0}}), .b(Result), .eq(comparator_1_eq), .lt(comparator_1_lt));  // open: gt
  Comparator #(.width(16)) comparator_2 (.a(Overflow), .b({16{Result[15]}}), .eq(comparator_2_eq));  // open: gt, lt
  not not_1 (not_1_out, comparator_2_eq);
  Flags_out flags_out_1 (
    .Sign_out(comparator_1_lt), .Zero_out(comparator_1_eq), .Overflow_out(not_1_out),
    .Carry_out(flags_in_1_carry_in), .Carry_block_out(flags_in_1_carry_block_in), .flag_out(flag_out));
endmodule

module Flags_in (
  input  [4:0] flag_in,
  output Sign_in,
  output Zero_in,
  output Overflow_in,
  output Carry_in,
  output Carry_block_in
);


  assign Carry_block_in = flag_in[4];
  assign Carry_in = flag_in[3];
  assign Overflow_in = flag_in[2];
  assign Sign_in = flag_in[0];
  assign Zero_in = flag_in[1];
endmodule

module Flags_out (
  input  Sign_out,
  input  Zero_out,
  input  Overflow_out,
  input  Carry_out,
  input  Carry_block_out,
  output [4:0] flag_out
);


  assign flag_out = {Carry_block_out, Carry_out, Overflow_out, Zero_out, Sign_out};
endmodule

module Expansion_Module (
  input  [3:0] in_1,
  output [15:0] out_2
);


  assign out_2 = {{12{1'b0}}, in_1};
endmodule

module Control_Unit (
  input  [3:0] Op_Code
);
endmodule

// add/sub
module Adder_Subtractor (
  input  Adder_Subtractor_Select,
  input  Carry_in,
  input  [15:0] a,
  input  [15:0] b,
  output [15:0] Output,
  output Overflow,
  output Carry_out
);

  wire adder_1_cout, adder_2_cout, adder_3_cout, adder_4_cout, adder_5_cout, adder_6_cout, adder_7_cout,
       adder_9_cout, adder_10_cout, adder_11_cout, adder_12_cout, adder_13_cout, adder_14_cout,
       adder_15_cout, multiplexer_1_out, multiplexer_2_out, multiplexer_3_out, multiplexer_4_out,
       multiplexer_5_out, multiplexer_6_out, multiplexer_7_out, multiplexer_8_out, multiplexer_9_out,
       multiplexer_10_out, multiplexer_11_out, multiplexer_12_out, multiplexer_13_out, multiplexer_14_out,
       multiplexer_15_out, multiplexer_16_out, not_1_out, not_2_out, not_3_out, not_4_out, not_5_out,
       not_6_out, not_7_out, not_8_out, not_9_out, not_10_out, not_11_out, not_12_out, not_13_out,
       not_14_out, not_15_out, not_16_out;

  not not_1 (not_1_out, a[0]);
  not not_2 (not_2_out, a[1]);
  not not_3 (not_3_out, a[2]);
  not not_4 (not_4_out, a[3]);
  not not_5 (not_5_out, a[4]);
  not not_6 (not_6_out, a[5]);
  not not_7 (not_7_out, a[6]);
  not not_8 (not_8_out, a[7]);
  not not_9 (not_9_out, a[8]);
  not not_10 (not_10_out, a[9]);
  not not_11 (not_11_out, a[10]);
  not not_12 (not_12_out, a[11]);
  not not_13 (not_13_out, a[12]);
  not not_14 (not_14_out, a[13]);
  not not_15 (not_15_out, a[14]);
  not not_16 (not_16_out, a[15]);
  Multiplexer #(.enable("false")) multiplexer_1 (
    .in0(a[0]), .in1(not_1_out), .out(multiplexer_1_out), .sel(Adder_Subtractor_Select));
  Multiplexer #(.enable("false")) multiplexer_2 (
    .in0(a[1]), .in1(not_2_out), .out(multiplexer_2_out), .sel(Adder_Subtractor_Select));
  Multiplexer #(.enable("false")) multiplexer_3 (
    .in0(a[2]), .in1(not_3_out), .out(multiplexer_3_out), .sel(Adder_Subtractor_Select));
  Multiplexer #(.enable("false")) multiplexer_4 (
    .in0(a[3]), .in1(not_4_out), .out(multiplexer_4_out), .sel(Adder_Subtractor_Select));
  Multiplexer #(.enable("false")) multiplexer_5 (
    .in0(a[4]), .in1(not_5_out), .out(multiplexer_5_out), .sel(Adder_Subtractor_Select));
  Multiplexer #(.enable("false")) multiplexer_6 (
    .in0(a[5]), .in1(not_6_out), .out(multiplexer_6_out), .sel(Adder_Subtractor_Select));
  Multiplexer #(.enable("false")) multiplexer_7 (
    .in0(a[6]), .in1(not_7_out), .out(multiplexer_7_out), .sel(Adder_Subtractor_Select));
  Multiplexer #(.enable("false")) multiplexer_8 (
    .in0(a[7]), .in1(not_8_out), .out(multiplexer_8_out), .sel(Adder_Subtractor_Select));
  Multiplexer #(.enable("false")) multiplexer_9 (
    .in0(a[8]), .in1(not_9_out), .out(multiplexer_9_out), .sel(Adder_Subtractor_Select));
  Multiplexer #(.enable("false")) multiplexer_10 (
    .in0(a[9]), .in1(not_10_out), .out(multiplexer_10_out), .sel(Adder_Subtractor_Select));
  Multiplexer #(.enable("false")) multiplexer_11 (
    .in0(a[10]), .in1(not_11_out), .out(multiplexer_11_out), .sel(Adder_Subtractor_Select));
  Multiplexer #(.enable("false")) multiplexer_12 (
    .in0(a[11]), .in1(not_12_out), .out(multiplexer_12_out), .sel(Adder_Subtractor_Select));
  Multiplexer #(.enable("false")) multiplexer_13 (
    .in0(a[12]), .in1(not_13_out), .out(multiplexer_13_out), .sel(Adder_Subtractor_Select));
  Multiplexer #(.enable("false")) multiplexer_14 (
    .in0(a[13]), .in1(not_14_out), .out(multiplexer_14_out), .sel(Adder_Subtractor_Select));
  Multiplexer #(.enable("false")) multiplexer_15 (
    .in0(a[14]), .in1(not_15_out), .out(multiplexer_15_out), .sel(Adder_Subtractor_Select));
  Multiplexer #(.enable("false")) multiplexer_16 (
    .in0(a[15]), .in1(not_16_out), .out(multiplexer_16_out), .sel(Adder_Subtractor_Select));
  Adder #(.width(1)) adder_1 (.a(multiplexer_1_out), .b(b[0]), .out(Output[0]), .cin(Carry_in), .cout(adder_1_cout));
  Adder #(.width(1)) adder_2 (
    .a(multiplexer_2_out), .b(a[6]), .out(Output[1]), .cin(adder_1_cout), .cout(adder_2_cout));
  Adder #(.width(1)) adder_3 (
    .a(multiplexer_3_out), .b(b[2]), .out(Output[2]), .cin(adder_2_cout), .cout(adder_3_cout));
  Adder #(.width(1)) adder_4 (
    .a(multiplexer_4_out), .b(b[3]), .out(Output[3]), .cin(adder_3_cout), .cout(adder_4_cout));
  Adder #(.width(1)) adder_5 (
    .a(multiplexer_5_out), .b(b[4]), .out(Output[4]), .cin(adder_4_cout), .cout(adder_5_cout));
  Adder #(.width(1)) adder_6 (
    .a(multiplexer_6_out), .b(b[5]), .out(Output[5]), .cin(adder_5_cout), .cout(adder_6_cout));
  Adder #(.width(1)) adder_7 (
    .a(multiplexer_7_out), .b(b[6]), .out(Output[6]), .cin(adder_6_cout), .cout(adder_7_cout));
  Adder #(.width(1)) adder_8 (.a(multiplexer_8_out), .b(b[7]), .out(Output[7]), .cin(adder_7_cout));  // open: cout
  Adder #(.width(1)) adder_9 (.a(multiplexer_9_out), .b(b[8]), .out(Output[8]), .cout(adder_9_cout));  // open: cin
  Adder #(.width(1)) adder_10 (
    .a(multiplexer_10_out), .b(b[9]), .out(Output[9]), .cin(adder_9_cout), .cout(adder_10_cout));
  Adder #(.width(1)) adder_11 (
    .a(multiplexer_11_out), .b(b[10]), .out(Output[10]), .cin(adder_10_cout), .cout(adder_11_cout));
  Adder #(.width(1)) adder_12 (
    .a(multiplexer_12_out), .b(b[11]), .out(Output[11]), .cin(adder_11_cout), .cout(adder_12_cout));
  Adder #(.width(1)) adder_13 (
    .a(multiplexer_13_out), .b(b[12]), .out(Output[12]), .cin(adder_12_cout), .cout(adder_13_cout));
  Adder #(.width(1)) adder_14 (
    .a(multiplexer_14_out), .b(b[13]), .out(Output[13]), .cin(adder_13_cout), .cout(adder_14_cout));
  Adder #(.width(1)) adder_15 (
    .a(multiplexer_15_out), .b(b[14]), .out(Output[14]), .cin(adder_14_cout), .cout(adder_15_cout));
  Adder #(.width(1)) adder_16 (
    .a(multiplexer_16_out), .b(b[15]), .out(Output[15]), .cin(adder_15_cout), .cout(Carry_out));
  xor xor_1 (Overflow, adder_15_cout, Carry_out);

  assign b[1] = a[6];
endmodule

module INC (
  input  [4:0] flag_in,
  input  [15:0] Data_a,
  input  [15:0] Data_b,
  output [4:0] flag_out,
  output [15:0] Data_d
);

  wire adder_1_cout, adder_subtractor_1_carry_out, adder_subtractor_1_overflow, flags_in_1_carry_block_in,
       flags_in_1_sign_in, flags_in_1_zero_in;
  wire [15:0] adder_1_out;

  Flags_in flags_in_1 (
    .flag_in(flag_in), .Sign_in(flags_in_1_sign_in), .Zero_in(flags_in_1_zero_in),
    .Carry_block_in(flags_in_1_carry_block_in));  // open: Overflow_in, Carry_in
  Adder #(.width(16)) adder_1 (.a(Data_b), .b(16'h1), .out(adder_1_out), .cin(1'b0), .cout(adder_1_cout));
  Adder_Subtractor adder_subtractor_1 (
    .a(Data_a), .b(adder_1_out), .Adder_Subtractor_Select(1'b0), .Carry_in(adder_1_cout),
    .Carry_out(adder_subtractor_1_carry_out), .Output(Data_d), .Overflow(adder_subtractor_1_overflow));
  Flags_out flags_out_1 (
    .Sign_out(flags_in_1_sign_in), .Zero_out(flags_in_1_zero_in), .Overflow_out(adder_subtractor_1_overflow),
    .Carry_out(adder_subtractor_1_carry_out), .Carry_block_out(flags_in_1_carry_block_in), .flag_out(flag_out));
endmodule

module SAVF (
  input  [4:0] flag_in,
  input  [15:0] Data_a,
  input  [15:0] Data_b,
  output [4:0] flag_out,
  output [15:0] Data_d
);

  Flags_in flags_in_1 (
    .flag_in(flag_in), .Sign_in(Data_d[0]), .Zero_in(Data_d[1]), .Overflow_in(Data_d[2]),
    .Carry_in(Data_d[3]), .Carry_block_in(Data_d[4]));
  Flags_out flags_out_1 (.flag_out(flag_out));  // open: Sign_out, Zero_out, Overflow_out, Carry_out, Carry_block_out

  assign Data_d[15:5] = {11{1'b0}};
endmodule

module DEC (
  input  [4:0] flag_in,
  input  [15:0] Data_a,
  input  [15:0] Data_b,
  output [4:0] flag_out,
  output [15:0] Data_d
);

  wire adder_1_cout, adder_subtractor_1_carry_out, adder_subtractor_1_overflow, flags_in_1_carry_block_in,
       flags_in_1_sign_in, flags_in_1_zero_in;
  wire [15:0] adder_1_out;

  Flags_in flags_in_1 (
    .flag_in(flag_in), .Sign_in(flags_in_1_sign_in), .Zero_in(flags_in_1_zero_in),
    .Carry_block_in(flags_in_1_carry_block_in));  // open: Overflow_in, Carry_in
  Adder #(.width(16)) adder_1 (.a(Data_b), .b(16'h1), .out(adder_1_out), .cin(1'b0), .cout(adder_1_cout));
  Adder_Subtractor adder_subtractor_1 (
    .a(Data_a), .b(adder_1_out), .Adder_Subtractor_Select(1'b1), .Carry_in(adder_1_cout),
    .Carry_out(adder_subtractor_1_carry_out), .Output(Data_d), .Overflow(adder_subtractor_1_overflow));
  Flags_out flags_out_1 (
    .Sign_out(flags_in_1_sign_in), .Zero_out(flags_in_1_zero_in), .Overflow_out(adder_subtractor_1_overflow),
    .Carry_out(adder_subtractor_1_carry_out), .Carry_block_out(flags_in_1_carry_block_in), .flag_out(flag_out));
endmodule

// Sign ext
module sign_extension (
  input  in_1,
  input  [7:0] in_2,
  output [15:0] out_3
);

  Multiplexer #(.width(16), .enable("false")) multiplexer_1 (
    .in0({{9{in_2[7]}}, in_2[6:0]}), .in1({in_2, {8{1'b0}}}), .out(out_3), .sel(in_1));
endmodule

module OR (
  input  [4:0] flag_in,
  input  [15:0] Data_a,
  input  [15:0] Data_b,
  output [4:0] flag_out,
  output [15:0] out
);

  wire comparator_1_eq, comparator_1_lt, flags_in_1_carry_block_in, flags_in_1_carry_in,
       flags_in_1_overflow_in;

  Flags_in flags_in_1 (
    .flag_in(flag_in), .Overflow_in(flags_in_1_overflow_in), .Carry_in(flags_in_1_carry_in),
    .Carry_block_in(flags_in_1_carry_block_in));  // open: Sign_in, Zero_in
  assign out = Data_a | Data_b;  // OR_Gate or_1, 16 bits wide
  Comparator #(.width(16)) comparator_1 (
    .a({16{1'b0}}), .b(out), .eq(comparator_1_eq), .lt(comparator_1_lt));  // open: gt
  Flags_out Flags_out (
    .Sign_out(comparator_1_lt), .Zero_out(comparator_1_eq), .Overflow_out(flags_in_1_overflow_in),
    .Carry_out(flags_in_1_carry_in), .Carry_block_out(flags_in_1_carry_block_in), .flag_out(flag_out));
endmodule

module RSTRF (
  input  [4:0] flag_in,
  input  [15:0] Data_a,
  input  [15:0] Data_b,
  output [4:0] flag_out,
  output [15:0] Data_d
);

  Flags_in flags_in_1 (.flag_in(flag_in));  // open: Sign_in, Zero_in, Overflow_in, Carry_in, Carry_block_in
  Flags_out flags_out_1 (.flag_out(flag_out));  // open: Sign_out, Zero_out, Overflow_out, Carry_out, Carry_block_out
endmodule
