// Logisim project Claire_W_Lab2_CircuitDesign.circ as structural Verilog: 1 circuit, main circuit main
module main (
  input  [2:0] ABC,
  output X,
  output Y
);

  wire A_prime_BC_ABC_out, AB_prime_C_ABC_out, ABC_prime_ABC_out, decoder_1_out3, decoder_1_out5,
       decoder_1_out6, decoder_1_out7, not_1_out;

  Decoder #(.select(3), .enable("false")) decoder_1 (
    .out3(decoder_1_out3), .out5(decoder_1_out5), .out6(decoder_1_out6), .out7(decoder_1_out7), .sel(ABC));  // open: out0, out1, out2, out4
  not not_1 (not_1_out, ABC[2]);
  Multiplexer #(.select(2), .enable("false")) multiplexer_1 (
    .in0(not_1_out), .in1(1'b0), .in2(1'b0), .in3(ABC[2]), .out(X), .sel(ABC[1:0]));
  or AB_prime_C_ABC (AB_prime_C_ABC_out, decoder_1_out5, decoder_1_out7);
  or A_prime_BC_ABC (A_prime_BC_ABC_out, decoder_1_out3, decoder_1_out7);
  or ABC_prime_ABC (ABC_prime_ABC_out, decoder_1_out6, decoder_1_out7);
  or or_1 (Y, AB_prime_C_ABC_out, A_prime_BC_ABC_out, ABC_prime_ABC_out);
endmodule
