// Logisim project Claire_W_Lab2_VendingMachine.circ as structural Verilog: 1 circuit, main circuit main
module main (
  input  [3:0] Q_D0_D1_D2,
  output Vend,
  output C0,
  output C1,
  output C2
);

  wire decoder_1_out1, decoder_1_out2, decoder_1_out3, decoder_1_out4, decoder_1_out5, decoder_1_out6,
       decoder_1_out7, decoder_1_out8, decoder_1_out9, decoder_1_out10, decoder_1_out11, decoder_1_out12,
       decoder_1_out13, decoder_1_out14, decoder_1_out15;

  Decoder #(.select(4), .enable("false")) decoder_1 (
    .out1(decoder_1_out1), .out2(decoder_1_out2), .out3(decoder_1_out3), .out4(decoder_1_out4),
    .out5(decoder_1_out5), .out6(decoder_1_out6), .out7(decoder_1_out7), .out8(decoder_1_out8),
    .out9(decoder_1_out9), .out10(decoder_1_out10), .out11(decoder_1_out11), .out12(decoder_1_out12),
    .out13(decoder_1_out13), .out14(decoder_1_out14), .out15(decoder_1_out15), .sel(Q_D0_D1_D2));  // open: out0
  or or_1 (Vend, decoder_1_out7, decoder_1_out9, decoder_1_out10, decoder_1_out11, decoder_1_out12, decoder_1_out13, decoder_1_out14, decoder_1_out15);
  or or_2 (C0, decoder_1_out3, decoder_1_out15, decoder_1_out5, decoder_1_out6, decoder_1_out8);
  or or_3 (C1, decoder_1_out1, decoder_1_out2, decoder_1_out4, decoder_1_out14, decoder_1_out13, decoder_1_out11);
  buf buffer_1 (C2, Q_D0_D1_D2[3]);
endmodule
