// Logisim project Lab3_Adder.circ as structural Verilog: 2 circuits, main circuit main
module main (
  input  Switch,
  input  [3:0] A,
  input  [3:0] B,
  output [3:0] Output,
  output Carry
);

  wire adder_1_cout, adder_2_cout, adder_3_cout, xor_1_out, xor_2_out, xor_3_out, xor_4_out;

  xor xor_1 (xor_1_out, Switch, B[2]);
  xor xor_2 (xor_2_out, Switch, B[3]);
  xor xor_3 (xor_3_out, Switch, B[0]);
  xor xor_4 (xor_4_out, Switch, B[1]);
  Adder #(.width(1)) adder_1 (.a(A[0]), .b(xor_3_out), .out(Output[0]), .cin(Switch), .cout(adder_1_cout));
  Adder #(.width(1)) adder_2 (.a(A[1]), .b(xor_4_out), .out(Output[1]), .cin(adder_1_cout), .cout(adder_2_cout));
  Adder #(.width(1)) adder_3 (.a(A[2]), .b(xor_1_out), .out(Output[2]), .cin(adder_2_cout), .cout(adder_3_cout));
  Adder #(.width(1)) adder_4 (.a(A[3]), .b(xor_2_out), .out(Output[3]), .cin(adder_3_cout), .cout(Carry));

  // Notes on the sheet:
  //   Adder-Subtractor
  //   This is an adder-subtractor circuit. I constructed the full adder with AND and OR and XOR in another file. It takes two one-bit inputs and gives a sum and a carry.
  //   To construct the subtractor, I used a switch which gives the negative signed value of B using two's complement
  //   When the switch is on, the circuit works as a subtractor; when the switch is off, the circuit is an adder.
endmodule

module Full_Adder (
  input  in_1,
  input  in_2,
  output out_3,
  output out_4
);

  wire and_1_out, and_2_out, and_3_out;

  and and_1 (and_1_out, in_1, in_2);
  and and_2 (and_2_out, and_1_out, in_1);
  and and_3 (and_3_out, and_1_out, in_2);
  ExactlyOne xor_1 (.out(out_3), .in0(in_1), .in1(and_1_out), .in2(in_2));
  or or_1 (out_4, and_2_out, and_1_out, and_3_out);
endmodule
