// Logisim project Lab3_VendingMachine.circ as structural Verilog: 1 circuit, main circuit main
module main (
  input  Quarter,
  input  Dime,
  input  Nickel,
  output Vend,
  output Nickel_2,
  output Dime_2,
  output _2Dimes
);

  wire and_1_out, and_2_out, and_3_out, and_4_out, and_5_out, and_6_out, and_9_out, CLK_out, decoder_1_out1,
       decoder_2_out1, decoder_2_out3, decoder_2_out5, decoder_2_out7, decoder_3_out1, decoder_3_out3,
       decoder_3_out5, decoder_3_out7, decoder_3_out9, decoder_4_out1, decoder_4_out2, decoder_4_out3,
       decoder_4_out4, decoder_4_out5, not_1_out, not_2_out, not_3_out, not_4_out, not_5_out, or_1_out,
       or_2_out, or_3_out, or_4_out, or_5_out, or_7_out, xor_1_out;
  wire [3:1] S2_q;

  Decoder #(.select(4), .enable("false")) decoder_1 (
    .out1(decoder_1_out1), .sel({S2_q, Quarter}));  // open: out0, out2, out3, out4, out5, out6, out7, out8, out9, out10, out11, out12, out13, out14, out15
  Decoder #(.select(4), .enable("false")) decoder_2 (
    .out1(decoder_2_out1), .out3(decoder_2_out3), .out5(decoder_2_out5), .out7(decoder_2_out7),
    .sel({S2_q, Dime}));  // open: out0, out2, out4, out6, out8, out9, out10, out11, out12, out13, out14, out15
  Decoder #(.select(4), .enable("false")) decoder_3 (
    .out1(decoder_3_out1), .out3(decoder_3_out3), .out5(decoder_3_out5), .out7(decoder_3_out7),
    .out9(decoder_3_out9), .sel({S2_q, Nickel}));  // open: out0, out2, out4, out6, out8, out10, out11, out12, out13, out14, out15
  or or_1 (or_1_out, decoder_1_out1, decoder_2_out7, decoder_3_out7, decoder_2_out5, decoder_3_out9);
  or or_2 (or_2_out, decoder_2_out1, decoder_2_out3, decoder_3_out3, decoder_3_out5);
  or or_3 (or_3_out, decoder_2_out3, decoder_1_out1, decoder_3_out1, decoder_3_out5, decoder_3_out9, decoder_2_out7);
  Clock CLK (.out(CLK_out));
  D_Flip_Flop S2 (.clk(CLK_out), .D(or_1_out), .Q(S2_q[3]));  // open: Qn, preset, en, reset
  D_Flip_Flop S1 (.clk(CLK_out), .D(or_2_out), .Q(S2_q[2]));  // open: Qn, preset, en, reset
  D_Flip_Flop S0 (.clk(CLK_out), .D(or_3_out), .Q(S2_q[1]));  // open: Qn, preset, en, reset
  Decoder #(.select(3), .enable("false")) decoder_4 (
    .out1(decoder_4_out1), .out2(decoder_4_out2), .out3(decoder_4_out3), .out4(decoder_4_out4),
    .out5(decoder_4_out5), .sel({S2_q[1], S2_q[2], S2_q[3]}));  // open: out0, out6, out7
  or or_4 (or_4_out, decoder_4_out1, decoder_4_out2, decoder_4_out3, decoder_4_out4, decoder_4_out5);
  and and_1 (and_1_out, or_4_out, Quarter);
  or or_5 (or_5_out, decoder_4_out4, decoder_4_out5);
  and and_2 (and_2_out, or_5_out, Dime);
  and and_3 (and_3_out, decoder_4_out5, Nickel);
  or or_6 (Vend, and_1_out, and_2_out, and_3_out);
  xor xor_1 (xor_1_out, S2_q[3], S2_q[2]);
  not not_1 (not_1_out, S2_q[1]);
  not not_2 (not_2_out, S2_q[2]);
  and and_4 (and_4_out, S2_q[3], not_2_out, S2_q[1], Dime);
  not not_3 (not_3_out, S2_q[3]);
  and and_5 (and_5_out, not_3_out, S2_q[2], S2_q[1]);
  not not_4 (not_4_out, S2_q[2]);
  and and_6 (and_6_out, not_4_out, S2_q[3], not_1_out);
  and and_7 (Dime_2, Quarter, or_7_out);
  or or_7 (or_7_out, and_6_out, and_5_out);
  not not_5 (not_5_out, S2_q[2]);
  and and_8 (_2Dimes, S2_q[3], not_5_out, Quarter, S2_q[1]);
  or or_8 (Nickel_2, and_4_out, and_9_out);
  and and_9 (and_9_out, xor_1_out, not_1_out, Quarter);

  // Notes on the sheet:
  //   The Vending machine takes quarters, dimes and nickels, one at a time
  //   When there are more than 30 cents in the machines, it vends and gives changes
  //   It does not give any changes when it does not vend
endmodule
