// Logisim project Term Project.circ as structural Verilog: 43 circuits, main circuit main
module main (
  input  clear,
  output [15:0] Next_PC,
  output [15:0] RAM_IN,
  output [3:0] Destination_addr,
  output [15:0] RAM_OUT,
  output [15:0] Rd_value
);

  wire Branch_Unit_flag_output, clock_out, control_unit_branch_en, control_unit_f_sel,
       control_unit_l_s_f__sel, control_unit_load_store_en, control_unit_memory_en, control_unit_r13_en,
       control_unit_ra_rd_sel, control_unit_ram_en, control_unit_reg_en, control_unit_set_clr_en,
       control_unit_set_en, control_unit_setlo_hi_sel, multiplexer_6_out, multiplexer_7_out;
  wire [1:0] control_unit_branch_sel;
  wire [3:0] control_unit_alu_op, multiplexer_2_out, multiplexer_8_out;
  wire [4:0] alsu_1_flag_out, control_unit_flag_en, flag_module_1_sign_out;
  wire [15:0] adder_1_out, alsu_1_r13_rt, Expansion_Module_out_4, multiplexer_3_out, multiplexer_4_out,
       multiplexer_5_out, register_1_q, register_file_1_data_b, rom_1_data, sign_extension_1_out_3;

  Clock clock (.out(clock_out));
  Control_Unit control_unit (
    ._15_0({rom_1_data[15:12], Destination_addr, rom_1_data[7:0]}),
    .LOAD_STORE_EN(control_unit_load_store_en), .L_S_F__SEL(control_unit_l_s_f__sel),
    .RA_RD_SEL(control_unit_ra_rd_sel), .MEMORY_EN(control_unit_memory_en),
    .SET_CLR_EN(control_unit_set_clr_en), .F_SEL(control_unit_f_sel), .R13_EN(control_unit_r13_en),
    .SETLO_HI_SEL(control_unit_setlo_hi_sel), .SET_EN(control_unit_set_en), .FLAG_EN(control_unit_flag_en),
    .REG_EN(control_unit_reg_en), .RAM_EN(control_unit_ram_en), .ALU_OP(control_unit_alu_op),
    .BRANCH_SEL(control_unit_branch_sel[0]), .BRANCH_EN(control_unit_branch_en));  // open: out_17, out_18
  Multiplexer #(.select(2), .width(16), .enable("false")) multiplexer_1 (
    .in0(adder_1_out), .in1(adder_1_out), .in2(multiplexer_5_out), .in3(register_file_1_data_b),
    .out(Next_PC), .sel(control_unit_branch_sel));
  Register #(.width(16)) register_1 (.D(Next_PC), .en(1'b1), .Q(register_1_q), .clk(clock_out), .clr(clear));
  Adder #(.width(16)) adder_1 (.a(16'h1), .b(register_1_q), .out(adder_1_out), .cin(1'b0));  // open: cout
  ROM #(.addrWidth(16), .dataWidth(16)) rom_1 (
    .addr(register_1_q), .data({rom_1_data[15:12], Destination_addr, rom_1_data[7:0]}));  // open: sel
  Expansion_Module Expansion_Module (
    .in_2(Destination_addr), .in_3({rom_1_data[12], rom_1_data[7:4]}), .in_1(control_unit_load_store_en),
    .out_4(Expansion_Module_out_4));
  Multiplexer #(.width(4), .enable("false")) multiplexer_2 (
    .in0(Destination_addr), .in1(rom_1_data[7:4]), .out(multiplexer_2_out), .sel(control_unit_ra_rd_sel));
  Register_File register_file_1 (
    .Data_In(multiplexer_5_out), .write_enable(control_unit_reg_en), .destination_addr(Destination_addr),
    .clear(clear), .regB_addr(rom_1_data[3:0]), .regA_addr(multiplexer_2_out), .Data_a(RAM_IN),
    .Data_b(register_file_1_data_b), .clock(clock_out), .R13(alsu_1_r13_rt), .R13_en(control_unit_r13_en));
  sign_extension sign_extension_1 (
    .out_3(sign_extension_1_out_3), .in_2(rom_1_data[7:0]), .in_1(control_unit_setlo_hi_sel));
  Multiplexer #(.width(16), .enable("false")) multiplexer_3 (
    .in0(Expansion_Module_out_4), .in1(RAM_IN), .out(multiplexer_3_out), .sel(control_unit_f_sel));
  Multiplexer #(.width(16), .enable("false")) multiplexer_4 (
    .in0(register_file_1_data_b), .in1(sign_extension_1_out_3), .out(multiplexer_4_out),
    .sel(control_unit_set_en));
  Multiplexer #(.width(16), .enable("false")) multiplexer_5 (
    .in0(Rd_value), .in1(RAM_OUT), .out(multiplexer_5_out), .sel(control_unit_memory_en));
  ALSU alsu_1 (
    .flag_in(flag_module_1_sign_out), .op(control_unit_alu_op), .Data_a(multiplexer_3_out),
    .Data_b(multiplexer_4_out), .flag_out(alsu_1_flag_out), .Data_d(Rd_value), .R13_Rt(alsu_1_r13_rt));
  Multiplexer #(.enable("false")) multiplexer_6 (
    .in0(rom_1_data[13]), .in1(alsu_1_flag_out[0]), .out(multiplexer_6_out), .sel(control_unit_l_s_f__sel));
  Multiplexer #(.enable("false")) multiplexer_7 (
    .in0(control_unit_flag_en[4]), .in1(Destination_addr[0]), .out(multiplexer_7_out),
    .sel(control_unit_set_clr_en));
  Multiplexer #(.width(4), .enable("false")) multiplexer_8 (
    .in0(control_unit_flag_en[3:0]), .in1(rom_1_data[3:0]), .out(multiplexer_8_out),
    .sel(control_unit_set_clr_en));
  Flag_Module flag_module_1 (
    .sign_out(flag_module_1_sign_out[0]), .zero_out(flag_module_1_sign_out[1]),
    .overflow_out(flag_module_1_sign_out[2]), .carry_out(flag_module_1_sign_out[3]),
    .carry_block_out(flag_module_1_sign_out[4]), .sign_in(multiplexer_6_out), .zero_in(alsu_1_flag_out[1]),
    .overflow_in(alsu_1_flag_out[2]), .carry_in(alsu_1_flag_out[3]), .carry_block_in(alsu_1_flag_out[4]),
    .SIGN_EN(multiplexer_8_out[0]), .ZERO_EN(multiplexer_8_out[1]), .OVERFLOW_EN(multiplexer_8_out[2]),
    .CARRYBLOCK_EN(multiplexer_7_out), .CARRY_EN(multiplexer_8_out[3]), .CLOCK(clock_out), .in_7(clear));
  LED sign (.in(alsu_1_flag_out[0]));
  LED zero (.in(alsu_1_flag_out[1]));
  LED overflow (.in(alsu_1_flag_out[2]));
  LED carry (.in(alsu_1_flag_out[3]));
  LED carry_block (.in(alsu_1_flag_out[4]));
  LED sign_2 (.in(flag_module_1_sign_out[0]));
  LED zero_2 (.in(flag_module_1_sign_out[1]));
  LED overflow_2 (.in(flag_module_1_sign_out[2]));
  LED carry_2 (.in(flag_module_1_sign_out[3]));
  LED carry_block_2 (.in(flag_module_1_sign_out[4]));
  Branch_Unit Branch_Unit (
    .flag_in(flag_module_1_sign_out), .op(Destination_addr), .flag_output(Branch_Unit_flag_output));
  and and_1 (control_unit_branch_sel[1], Branch_Unit_flag_output, control_unit_branch_en);
  RAM #(.addrWidth(16), .dataWidth(16), .bus("separate")) ram_1 (
    .addr(Rd_value), .din(RAM_IN), .data(RAM_OUT), .str(control_unit_ram_en), .sel(1'b1), .clk(clock_out),
    .ld(1'b1), .clr(clear));

  // Notes on the sheet:
  //   contents of rom_1 (hex, n*v repeats v):
  //   3160 e101 f100 e202 f200 3068 b020 ed0f fd00 140d c112 32c0 ed0a fd00 150d e307 f300 6103
  //   RAM
endmodule

// Reigister File
module Register_File (
  input  [15:0] Data_In,
  input  write_enable,
  input  [3:0] destination_addr,
  input  [15:0] R13,
  input  R13_en,
  input  clear,
  input  clock,
  input  [3:0] regB_addr,
  input  [3:0] regA_addr,
  output [15:0] Data_a,
  output [15:0] Data_b
);

  wire decoder_1_out0, decoder_1_out1, decoder_1_out2, decoder_1_out3, decoder_1_out4, decoder_1_out5,
       decoder_1_out6, decoder_1_out7, decoder_1_out8, decoder_1_out9, decoder_1_out10, decoder_1_out11,
       decoder_1_out12, decoder_1_out13, decoder_1_out14, decoder_1_out15;
  wire [15:0] multiplexer_1_out, R0_q, R1_q, R2_q, R3_q, R4_q, R5_q, R6_q, R7_q, R8_q, R9_q, R10_q, R11_q,
       R12_q, R13_q, R14_q, R15_q;

  Decoder #(.select(4), .disabled(0)) decoder_1 (
    .out0(decoder_1_out0), .out1(decoder_1_out1), .out2(decoder_1_out2), .out3(decoder_1_out3),
    .out4(decoder_1_out4), .out5(decoder_1_out5), .out6(decoder_1_out6), .out7(decoder_1_out7),
    .out8(decoder_1_out8), .out9(decoder_1_out9), .out10(decoder_1_out10), .out11(decoder_1_out11),
    .out12(decoder_1_out12), .out13(decoder_1_out13), .out14(decoder_1_out14), .out15(decoder_1_out15),
    .sel(destination_addr), .en(write_enable));
  Register #(.width(16)) R0 (.D({16{1'b0}}), .en(decoder_1_out0), .Q(R0_q), .clk(clock), .clr(clear));
  Register #(.width(16)) R2 (.D(Data_In), .en(decoder_1_out2), .Q(R2_q), .clk(clock), .clr(clear));
  Register #(.width(16)) R4 (.D(Data_In), .en(decoder_1_out4), .Q(R4_q), .clk(clock), .clr(clear));
  Register #(.width(16)) R6 (.D(Data_In), .en(decoder_1_out6), .Q(R6_q), .clk(clock), .clr(clear));
  Register #(.width(16)) R8 (.D(Data_In), .en(decoder_1_out8), .Q(R8_q), .clk(clock), .clr(clear));
  Register #(.width(16)) R10 (.D(Data_In), .en(decoder_1_out10), .Q(R10_q), .clk(clock), .clr(clear));
  Register #(.width(16)) R12 (.D(Data_In), .en(decoder_1_out12), .Q(R12_q), .clk(clock), .clr(clear));
  Register #(.width(16)) R14 (.D(Data_In), .en(decoder_1_out14), .Q(R14_q), .clk(clock), .clr(clear));
  Multiplexer #(.width(16), .enable("false")) multiplexer_1 (
    .in0(Data_In), .in1(R13), .out(multiplexer_1_out), .sel(R13_en));
  Register #(.width(16)) R1 (.D(Data_In), .en(decoder_1_out1), .Q(R1_q), .clk(clock), .clr(clear));
  Register #(.width(16)) R3 (.D(Data_In), .en(decoder_1_out3), .Q(R3_q), .clk(clock), .clr(clear));
  Register #(.width(16)) R5 (.D(Data_In), .en(decoder_1_out5), .Q(R5_q), .clk(clock), .clr(clear));
  Register #(.width(16)) R7 (.D(Data_In), .en(decoder_1_out7), .Q(R7_q), .clk(clock), .clr(clear));
  Register #(.width(16)) R9 (.D(Data_In), .en(decoder_1_out9), .Q(R9_q), .clk(clock), .clr(clear));
  Register #(.width(16)) R11 (.D(Data_In), .en(decoder_1_out11), .Q(R11_q), .clk(clock), .clr(clear));
  Register #(.width(16)) u_R13 (.D(multiplexer_1_out), .en(decoder_1_out13), .Q(R13_q), .clk(clock), .clr(clear));
  Register #(.width(16)) R15 (.D(Data_In), .en(decoder_1_out15), .Q(R15_q), .clk(clock), .clr(clear));
  Multiplexer #(.select(4), .width(16), .enable("false")) multiplexer_2 (
    .in0(R0_q), .in1(R1_q), .in2(R2_q), .in3(R3_q), .in4(R4_q), .in5(R5_q), .in6(R6_q), .in7(R7_q),
    .in8(R8_q), .in9(R9_q), .in10(R10_q), .in11(R11_q), .in12(R12_q), .in13(R13_q), .in14(R14_q),
    .in15(R15_q), .out(Data_a), .sel(regA_addr));
  Multiplexer #(.select(4), .width(16), .enable("false")) multiplexer_3 (
    .in0(R0_q), .in1(R1_q), .in2(R2_q), .in3(R3_q), .in4(R4_q), .in5(R5_q), .in6(R6_q), .in7(R7_q),
    .in8(R8_q), .in9(R9_q), .in10(R10_q), .in11(R11_q), .in12(R12_q), .in13(R13_q), .in14(R14_q),
    .in15(R15_q), .out(Data_b), .sel(regB_addr));

  // Notes on the sheet:
  //   sixteen 16-bit Register file
endmodule

module ALSU (
  input  [4:0] flag_in,
  input  [3:0] op,
  input  [15:0] Data_a,
  input  [15:0] Data_b,
  output [4:0] flag_out,
  output [15:0] Data_d,
  output [15:0] R13_Rt
);

  wire [4:0] add_1_flag_out, and_1_flag_out, clrf_1_flag_out, dec_1_flag_out, inc_1_flag_out, lsl_1_flag_out,
       lsr_1_flag_out, mult_1_flag_out, or_1_flag_out, setf_1_flag_out, sethi_1_flag_out, setlo_1_flag_out,
       sub_1_flag_out, xor_1_flag_out;
  wire [15:0] add_1_data_d, and_1_out, clrf_1_data_d, dec_1_data_d, inc_1_data_d, lsl_1_data_d, lsr_1_data_d,
       mult_1_result, or_1_out, setf_1_data_d, sethi_1_data_d, setlo_1_data_d, sub_1_data_d, xor_1_data_d;

  SETLO setlo_1 (
    .flag_in(flag_in), .Data_a(Data_a), .Data_b(Data_b), .flag_out(setlo_1_flag_out), .Data_d(setlo_1_data_d));
  AND and_1 (.flag_in(flag_in), .Data_a(Data_a), .Data_b(Data_b), .flag_out(and_1_flag_out), .out(and_1_out));
  OR or_1 (.flag_in(flag_in), .Data_a(Data_a), .Data_b(Data_b), .flag_out(or_1_flag_out), .out(or_1_out));
  ADD add_1 (.flag_in(flag_in), .Data_a(Data_a), .Data_b(Data_b), .flag_out(add_1_flag_out), .Data_d(add_1_data_d));
  SUB sub_1 (.flag_in(flag_in), .Data_a(Data_a), .Data_b(Data_b), .flag_out(sub_1_flag_out), .Data_d(sub_1_data_d));
  MULT mult_1 (
    .flag_in(flag_in), .Data_a(Data_a), .Data_b(Data_b), .flag_out(mult_1_flag_out), .Result(mult_1_result),
    .Overflow(R13_Rt));
  XOR xor_1 (.flag_in(flag_in), .Data_a(Data_a), .Data_b(Data_b), .flag_out(xor_1_flag_out), .Data_d(xor_1_data_d));
  LSL lsl_1 (.flag_in(flag_in), .Data_a(Data_a), .Data_b(Data_b), .flag_out(lsl_1_flag_out), .Data_d(lsl_1_data_d));
  LSR lsr_1 (.flag_in(flag_in), .Data_a(Data_a), .Data_b(Data_b), .flag_out(lsr_1_flag_out), .Data_d(lsr_1_data_d));
  SETF setf_1 (.flag_in(flag_in), .Data_a(Data_a), .Data_b(Data_b), .flag_out(setf_1_flag_out), .Data_d(setf_1_data_d));
  CLRF clrf_1 (.flag_in(flag_in), .Data_a(Data_a), .Data_b(Data_b), .flag_out(clrf_1_flag_out), .Data_d(clrf_1_data_d));
  SETHI sethi_1 (
    .flag_in(flag_in), .Data_a(Data_a), .Data_b(Data_b), .flag_out(sethi_1_flag_out), .Data_d(sethi_1_data_d));
  INC inc_1 (.flag_in(flag_in), .Data_a(Data_a), .Data_b(Data_b), .flag_out(inc_1_flag_out), .Data_d(inc_1_data_d));
  DEC dec_1 (.flag_in(flag_in), .Data_a(Data_a), .Data_b(Data_b), .flag_out(dec_1_flag_out), .Data_d(dec_1_data_d));
  MUX mux_1 (
    .flag0(setlo_1_flag_out), .In0(setlo_1_data_d), .flag1(and_1_flag_out), .In1(and_1_out),
    .flag2(or_1_flag_out), .In2(or_1_out), .flag3(add_1_flag_out), .In3(add_1_data_d),
    .flag4(sub_1_flag_out), .In4(sub_1_data_d), .flag5(mult_1_flag_out), .In5(mult_1_result),
    .flag6(xor_1_flag_out), .In6(xor_1_data_d), .flag7(lsl_1_flag_out), .In7(lsl_1_data_d),
    .flag8(lsr_1_flag_out), .In8(lsr_1_data_d), .flag9(setf_1_flag_out), .In9(setf_1_data_d),
    .flag10(clrf_1_flag_out), .In10(clrf_1_data_d), .flag11(sethi_1_flag_out), .In11(sethi_1_data_d),
    .flag12(inc_1_flag_out), .In12(inc_1_data_d), .flag13(dec_1_flag_out), .In13(dec_1_data_d),
    .flag_out(flag_out), .\output (Data_d), .op(op));  // open: flag14, In14, flag15, In15
endmodule

module SETLO (
  input  [4:0] flag_in,
  input  [15:0] Data_a,
  input  [15:0] Data_b,
  output [4:0] flag_out,
  output [15:0] Data_d
);

  wire flags_in_1_carry_block_in, flags_in_1_carry_in, flags_in_1_overflow_in, flags_in_1_sign_in,
       flags_in_1_zero_in;

  Flags_in flags_in_1 (
    .flag_in(flag_in), .Sign_in(flags_in_1_sign_in), .Zero_in(flags_in_1_zero_in),
    .Overflow_in(flags_in_1_overflow_in), .Carry_in(flags_in_1_carry_in),
    .Carry_block_in(flags_in_1_carry_block_in));
  Flags_out flags_out_1 (
    .Sign_out(flags_in_1_sign_in), .Zero_out(flags_in_1_zero_in), .Overflow_out(flags_in_1_overflow_in),
    .Carry_out(flags_in_1_carry_in), .Carry_block_out(flags_in_1_carry_block_in), .flag_out(flag_out));

  assign Data_d = Data_b;
endmodule

module ADD (
  input  [4:0] flag_in,
  input  [15:0] Data_a,
  input  [15:0] Data_b,
  output [4:0] flag_out,
  output [15:0] Data_d
);

  wire Adder_carry_out, Adder_overflow, and_1_out, comparator_1_eq, comparator_1_gt, Flags_in_carry_block_in,
       Flags_in_carry_in, not_1_out;

  Flags_in Flags_in (
    .flag_in(flag_in), .Carry_in(Flags_in_carry_in), .Carry_block_in(Flags_in_carry_block_in));  // open: Sign_in, Zero_in, Overflow_in
  and and_1 (and_1_out, Flags_in_carry_in, not_1_out);
  not not_1 (not_1_out, Flags_in_carry_block_in);
  Adder_Subtractor Adder (
    .a(Data_b), .b(Data_a), .Output(Data_d), .Overflow(Adder_overflow), .Adder_Subtractor_Select(1'b0),
    .Carry_in(and_1_out), .Carry_out(Adder_carry_out));
  Comparator #(.width(16)) comparator_1 (
    .a({16{1'b0}}), .b(Data_d), .gt(comparator_1_gt), .eq(comparator_1_eq));  // open: lt
  Flags_out Flags_out (
    .Sign_out(comparator_1_gt), .Zero_out(comparator_1_eq), .Overflow_out(Adder_overflow),
    .Carry_out(Adder_carry_out), .Carry_block_out(Flags_in_carry_block_in), .flag_out(flag_out));
endmodule

module MUX (
  input  [3:0] op,
  input  [4:0] flag0,
  input  [15:0] In0,
  input  [4:0] flag1,
  input  [15:0] In1,
  input  [4:0] flag2,
  input  [15:0] In2,
  input  [4:0] flag3,
  input  [15:0] In3,
  input  [4:0] flag4,
  input  [15:0] In4,
  input  [4:0] flag5,
  input  [15:0] In5,
  input  [4:0] flag6,
  input  [15:0] In6,
  input  [4:0] flag7,
  input  [15:0] In7,
  input  [4:0] flag8,
  input  [15:0] In8,
  input  [4:0] flag9,
  input  [15:0] In9,
  input  [4:0] flag10,
  input  [15:0] In10,
  input  [4:0] flag11,
  input  [15:0] In11,
  input  [4:0] flag12,
  input  [15:0] In12,
  input  [4:0] flag13,
  input  [15:0] In13,
  input  [4:0] flag14,
  input  [15:0] In14,
  input  [4:0] flag15,
  input  [15:0] In15,
  output [4:0] flag_out,
  output [15:0] \output 
);

  Multiplexer #(.select(4), .width(5), .enable("false")) multiplexer_1 (
    .in0(flag0), .in1(flag1), .in2(flag2), .in3(flag3), .in4(flag4), .in5(flag5), .in6(flag6), .in7(flag7),
    .in8(flag8), .in9(flag9), .in10(flag10), .in11(flag11), .in12(flag12), .in13(flag13), .in14(flag14),
    .in15(flag15), .out(flag_out), .sel(op));
  Multiplexer #(.select(4), .width(16), .enable("false")) multiplexer_2 (
    .in0(In0), .in1(In1), .in2(In2), .in3(In3), .in4(In4), .in5(In5), .in6(In6), .in7(In7), .in8(In8),
    .in9(In9), .in10(In10), .in11(In11), .in12(In12), .in13(In13), .in14(In14), .in15(In15), .out(\output ),
    .sel(op));
endmodule

module AND (
  input  [4:0] flag_in,
  input  [15:0] Data_a,
  input  [15:0] Data_b,
  output [4:0] flag_out,
  output [15:0] out
);

  wire comparator_1_eq, comparator_1_gt, flags_in_1_carry_block_in, flags_in_1_carry_in,
       flags_in_1_overflow_in;

  Flags_in flags_in_1 (
    .flag_in(flag_in), .Overflow_in(flags_in_1_overflow_in), .Carry_in(flags_in_1_carry_in),
    .Carry_block_in(flags_in_1_carry_block_in));  // open: Sign_in, Zero_in
  assign out = Data_a & Data_b;  // AND_Gate and_1, 16 bits wide
  Comparator #(.width(16)) comparator_1 (
    .a({16{1'b0}}), .b(out), .gt(comparator_1_gt), .eq(comparator_1_eq));  // open: lt
  Flags_out Flags_out (
    .Sign_out(comparator_1_gt), .Zero_out(comparator_1_eq), .Overflow_out(flags_in_1_overflow_in),
    .Carry_out(flags_in_1_carry_in), .Carry_block_out(flags_in_1_carry_block_in), .flag_out(flag_out));
endmodule

module Flag_Module (
  input  sign_in,
  input  zero_in,
  input  overflow_in,
  input  carry_in,
  input  carry_block_in,
  input  CLOCK,
  input  in_7,
  input  SIGN_EN,
  input  ZERO_EN,
  input  OVERFLOW_EN,
  input  CARRYBLOCK_EN,
  input  CARRY_EN,
  output sign_out,
  output zero_out,
  output overflow_out,
  output carry_out,
  output carry_block_out
);

  D_Flip_Flop F0 (.clk(CLOCK), .D(sign_in), .Q(sign_out), .preset(1'b0), .en(SIGN_EN), .reset(in_7));  // open: Qn
  D_Flip_Flop F1 (.clk(CLOCK), .D(zero_in), .Q(zero_out), .preset(1'b0), .en(ZERO_EN), .reset(in_7));  // open: Qn
  D_Flip_Flop F2 (
    .clk(CLOCK), .D(overflow_in), .Q(overflow_out), .preset(1'b0), .en(OVERFLOW_EN), .reset(in_7));  // open: Qn
  D_Flip_Flop F3 (.clk(CLOCK), .D(carry_in), .Q(carry_out), .preset(1'b0), .en(CARRY_EN), .reset(in_7));  // open: Qn
  D_Flip_Flop F4 (
    .clk(CLOCK), .D(carry_block_in), .Q(carry_block_out), .preset(1'b0), .en(CARRYBLOCK_EN), .reset(in_7));  // open: Qn
endmodule

module SUB (
  input  [4:0] flag_in,
  input  [15:0] Data_a,
  input  [15:0] Data_b,
  output [4:0] flag_out,
  output [15:0] Data_d
);

  wire comparator_1_eq, comparator_1_gt, Flags_in_carry_block_in, Flags_in_carry_in, nand_1_out, not_1_out,
       not_2_out, Sub_carry_out, Sub_overflow;

  Flags_in Flags_in (
    .flag_in(flag_in), .Carry_in(Flags_in_carry_in), .Carry_block_in(Flags_in_carry_block_in));  // open: Sign_in, Zero_in, Overflow_in
  not not_1 (not_1_out, Flags_in_carry_in);
  not not_2 (not_2_out, Flags_in_carry_block_in);
  nand nand_1 (nand_1_out, not_1_out, not_2_out);
  Adder_Subtractor Sub (
    .a(Data_b), .b(Data_a), .Output(Data_d), .Overflow(Sub_overflow), .Adder_Subtractor_Select(1'b1),
    .Carry_in(nand_1_out), .Carry_out(Sub_carry_out));
  Comparator #(.width(16)) comparator_1 (
    .a({16{1'b0}}), .b(Data_d), .gt(comparator_1_gt), .eq(comparator_1_eq));  // open: lt
  Flags_out Flags_out (
    .Sign_out(comparator_1_gt), .Zero_out(comparator_1_eq), .Overflow_out(Sub_overflow),
    .Carry_out(Sub_carry_out), .Carry_block_out(Flags_in_carry_block_in), .flag_out(flag_out));
endmodule

module LSL (
  input  [4:0] flag_in,
  input  [15:0] Data_a,
  input  [15:0] Data_b,
  output [4:0] flag_out,
  output [15:0] Data_d
);

  wire Flags_in_carry_block_in, Flags_in_carry_in, Flags_in_sign_in, Flags_in_zero_in, not_1_out, xor_1_out;

  Flags_in Flags_in (
    .flag_in(flag_in), .Sign_in(Flags_in_sign_in), .Zero_in(Flags_in_zero_in), .Carry_in(Flags_in_carry_in),
    .Carry_block_in(Flags_in_carry_block_in));  // open: Overflow_in
  not not_1 (not_1_out, Flags_in_carry_in);
  and and_1 (Data_d[0], not_1_out, Flags_in_carry_block_in);
  xor xor_1 (xor_1_out, Data_b[14], Data_b[15]);
  Flags_out flags_out (
    .Sign_out(Flags_in_sign_in), .Zero_out(Flags_in_zero_in), .Overflow_out(xor_1_out),
    .Carry_out(Data_b[15]), .Carry_block_out(Flags_in_carry_block_in), .flag_out(flag_out));

  assign Data_d[15:1] = Data_b[14:0];
endmodule

module LSR (
  input  [4:0] flag_in,
  input  [15:0] Data_a,
  input  [15:0] Data_b,
  output [4:0] flag_out,
  output [15:0] Data_d
);

  wire Flags_in_carry_block_in, Flags_in_carry_in, Flags_in_overflow_in, Flags_in_sign_in, Flags_in_zero_in,
       not_1_out;

  Flags_in Flags_in (
    .flag_in(flag_in), .Sign_in(Flags_in_sign_in), .Zero_in(Flags_in_zero_in),
    .Overflow_in(Flags_in_overflow_in), .Carry_in(Flags_in_carry_in), .Carry_block_in(Flags_in_carry_block_in));
  and and_1 (Data_d[15], Flags_in_carry_in, not_1_out);
  not not_1 (not_1_out, Flags_in_carry_block_in);
  Flags_out flags_out (
    .Sign_out(Flags_in_sign_in), .Zero_out(Flags_in_zero_in), .Overflow_out(Flags_in_overflow_in),
    .Carry_out(Data_b[0]), .Carry_block_out(not_1_out), .flag_out(flag_out));

  assign Data_d[14:0] = Data_b[15:1];
endmodule

module SETF (
  input  [4:0] flag_in,
  input  [15:0] Data_a,
  input  [15:0] Data_b,
  output [4:0] flag_out,
  output [15:0] Data_d
);

  Flags_in flags_in_1 (.flag_in(flag_in));  // open: Sign_in, Zero_in, Overflow_in, Carry_in, Carry_block_in
  Flags_out flags_out_1 (
    .Sign_out(1'b1), .Zero_out(1'b1), .Overflow_out(1'b1), .Carry_out(1'b1), .Carry_block_out(1'b1),
    .flag_out(flag_out));

  assign Data_d = {16{1'b0}};
endmodule

module XOR (
  input  [4:0] flag_in,
  input  [15:0] Data_a,
  input  [15:0] Data_b,
  output [4:0] flag_out,
  output [15:0] Data_d
);

  wire comparator_1_eq, comparator_1_gt, flags_in_1_carry_block_in, flags_in_1_carry_in,
       flags_in_1_overflow_in;

  Flags_in flags_in_1 (
    .flag_in(flag_in), .Overflow_in(flags_in_1_overflow_in), .Carry_in(flags_in_1_carry_in),
    .Carry_block_in(flags_in_1_carry_block_in));  // open: Sign_in, Zero_in
  assign Data_d = Data_a ^ Data_b;  // XOR_Gate xor_1, 16 bits wide
  Comparator #(.width(16)) comparator_1 (
    .a({16{1'b0}}), .b(Data_d), .gt(comparator_1_gt), .eq(comparator_1_eq));  // open: lt
  Flags_out Flags_out (
    .Sign_out(comparator_1_gt), .Zero_out(comparator_1_eq), .Overflow_out(flags_in_1_overflow_in),
    .Carry_out(flags_in_1_carry_in), .Carry_block_out(flags_in_1_carry_block_in), .flag_out(flag_out));
endmodule

module MULT (
  input  [4:0] flag_in,
  input  [15:0] Data_a,
  input  [15:0] Data_b,
  output [4:0] flag_out,
  output [15:0] Result,
  output [15:0] Overflow
);

  wire comparator_1_eq, comparator_1_gt, comparator_2_eq, flags_in_1_carry_block_in, flags_in_1_carry_in,
       not_1_out;

  Flags_in flags_in_1 (
    .flag_in(flag_in), .Carry_in(flags_in_1_carry_in), .Carry_block_in(flags_in_1_carry_block_in));  // open: Sign_in, Zero_in, Overflow_in
  Multiplier #(.width(16)) multiplier_1 (.a(Data_a), .b(Data_b), .out(Result), .cout(Overflow));  // open: cin
  Comparator #(.width(16)) comparator_1 (
    .a({16{1'b0}}), .b(Result), .gt(comparator_1_gt), .eq(comparator_1_eq));  // open: lt
  Comparator #(.width(16)) comparator_2 (.a(Overflow), .b({16{Result[15]}}), .eq(comparator_2_eq));  // open: gt, lt
  not not_1 (not_1_out, comparator_2_eq);
  Flags_out flags_out_1 (
    .Sign_out(comparator_1_gt), .Zero_out(comparator_1_eq), .Overflow_out(not_1_out),
    .Carry_out(flags_in_1_carry_in), .Carry_block_out(flags_in_1_carry_block_in), .flag_out(flag_out));
endmodule

module Flags_in (
  input  [4:0] flag_in,
  output Sign_in,
  output Zero_in,
  output Overflow_in,
  output Carry_in,
  output Carry_block_in
);


  assign Carry_block_in = flag_in[4];
  assign Carry_in = flag_in[3];
  assign Overflow_in = flag_in[2];
  assign Sign_in = flag_in[0];
  assign Zero_in = flag_in[1];
endmodule

module Flags_out (
  input  Sign_out,
  input  Zero_out,
  input  Overflow_out,
  input  Carry_out,
  input  Carry_block_out,
  output [4:0] flag_out
);


  assign flag_out = {Carry_block_out, Carry_out, Overflow_out, Zero_out, Sign_out};
endmodule

module Expansion_Module (
  input  in_1,
  input  [3:0] in_2,
  input  [4:0] in_3,
  output [15:0] out_4
);

  Multiplexer #(.width(16), .enable("false")) multiplexer_1 (
    .in0({{12{1'b0}}, in_2}), .in1({{11{1'b0}}, in_3}), .out(out_4), .sel(in_1));
endmodule

module Control_Unit (
  input  [15:0] _15_0,
  output LOAD_STORE_EN,
  output L_S_F__SEL,
  output RA_RD_SEL,
  output MEMORY_EN,
  output SET_CLR_EN,
  output F_SEL,
  output R13_EN,
  output SETLO_HI_SEL,
  output SET_EN,
  output [4:0] FLAG_EN,
  output REG_EN,
  output RAM_EN,
  output [3:0] ALU_OP,
  output BRANCH_SEL,
  output BRANCH_EN,
  output out_17,
  output out_18
);

  wire and_1_out, and_2_out, and_3_out;
  wire [0:0] multiplexer_1_out;
  wire [23:0] multiplexer_2_out, multiplexer_3_out, rom_1_data, rom_2_data, rom_3_data, rom_4_data;

  and and_1 (and_1_out, ~_15_0[15], ~_15_0[14], _15_0[13], ~_15_0[12]);  // AND_Gate
  and and_2 (and_2_out, ~_15_0[15], ~_15_0[14], _15_0[13], _15_0[12]);  // AND_Gate
  and and_3 (and_3_out, ~_15_0[7], _15_0[6], _15_0[5]);  // AND_Gate
  Multiplexer #(.enable("false")) multiplexer_1 (
    .in0(_15_0[11]), .in1(_15_0[3]), .out(multiplexer_1_out[0]), .sel(_15_0[4]));
  ROM #(.addrWidth(4), .dataWidth(24)) rom_1 (.addr(_15_0[15:12]), .data(rom_1_data));  // open: sel
  ROM #(.addrWidth(4), .dataWidth(24)) rom_2 (.addr(_15_0[7:4]), .data(rom_2_data));  // open: sel
  ROM #(.addrWidth(2), .dataWidth(24)) rom_3 (.addr({_15_0[4], multiplexer_1_out[0]}), .data(rom_3_data));  // open: sel
  ROM #(.addrWidth(2), .dataWidth(24)) rom_4 (.addr({1'b0, _15_0[8]}), .data(rom_4_data));  // open: sel
  Multiplexer #(.width(24), .enable("false")) multiplexer_2 (
    .in0(rom_2_data), .in1(rom_3_data), .out(multiplexer_2_out), .sel(and_3_out));
  Multiplexer #(.width(24), .enable("false")) multiplexer_3 (
    .in0(rom_1_data), .in1(multiplexer_2_out), .out(multiplexer_3_out), .sel(and_2_out));
  Multiplexer #(.width(24), .enable("false")) multiplexer_4 (
    .in0(multiplexer_3_out), .in1(rom_4_data),
    .out({out_18, out_17, BRANCH_EN, BRANCH_SEL, ALU_OP, RAM_EN, REG_EN, FLAG_EN, SET_EN, SETLO_HI_SEL, R13_EN, F_SEL, SET_CLR_EN, MEMORY_EN, RA_RD_SEL, L_S_F__SEL, LOAD_STORE_EN}),
    .sel(and_1_out));

  // Notes on the sheet:
  //   contents of rom_1 (hex, n*v repeats v):
  //   234100 334000 34000 0 34609 34609 38001 38001 14626 24626 35e26 45e26 54e66 64626 4126 b4122
  //   contents of rom_2 (hex, n*v repeats v):
  //   75806 85806 6*0 4*c5e22 4*d5e22
  //   contents of rom_3 (hex, n*v repeats v):
  //   90036 a0036
endmodule

// add/sub
module Adder_Subtractor (
  input  Adder_Subtractor_Select,
  input  Carry_in,
  input  [15:0] a,
  input  [15:0] b,
  output [15:0] Output,
  output Overflow,
  output Carry_out
);

  wire adder_1_cout, adder_2_cout, adder_3_cout, adder_4_cout, adder_5_cout, adder_6_cout, adder_7_cout,
       adder_8_cout, adder_9_cout, adder_10_cout, adder_11_cout, adder_12_cout, adder_13_cout, adder_14_cout,
       adder_15_cout, multiplexer_1_out, multiplexer_2_out, multiplexer_3_out, multiplexer_4_out,
       multiplexer_5_out, multiplexer_6_out, multiplexer_7_out, multiplexer_8_out, multiplexer_9_out,
       multiplexer_10_out, multiplexer_11_out, multiplexer_12_out, multiplexer_13_out, multiplexer_14_out,
       multiplexer_15_out, multiplexer_16_out, not_1_out, not_2_out, not_3_out, not_4_out, not_5_out,
       not_6_out, not_7_out, not_8_out, not_9_out, not_10_out, not_11_out, not_12_out, not_13_out,
       not_14_out, not_15_out, not_16_out;

  not not_1 (not_1_out, a[0]);
  not not_2 (not_2_out, a[1]);
  not not_3 (not_3_out, a[2]);
  not not_4 (not_4_out, a[3]);
  not not_5 (not_5_out, a[4]);
  not not_6 (not_6_out, a[5]);
  not not_7 (not_7_out, a[6]);
  not not_8 (not_8_out, a[7]);
  not not_9 (not_9_out, a[8]);
  not not_10 (not_10_out, a[9]);
  not not_11 (not_11_out, a[10]);
  not not_12 (not_12_out, a[11]);
  not not_13 (not_13_out, a[12]);
  not not_14 (not_14_out, a[13]);
  not not_15 (not_15_out, a[14]);
  not not_16 (not_16_out, a[15]);
  Multiplexer #(.enable("false")) multiplexer_1 (
    .in0(a[0]), .in1(not_1_out), .out(multiplexer_1_out), .sel(Adder_Subtractor_Select));
  Multiplexer #(.enable("false")) multiplexer_2 (
    .in0(a[1]), .in1(not_2_out), .out(multiplexer_2_out), .sel(Adder_Subtractor_Select));
  Multiplexer #(.enable("false")) multiplexer_3 (
    .in0(a[2]), .in1(not_3_out), .out(multiplexer_3_out), .sel(Adder_Subtractor_Select));
  Multiplexer #(.enable("false")) multiplexer_4 (
    .in0(a[3]), .in1(not_4_out), .out(multiplexer_4_out), .sel(Adder_Subtractor_Select));
  Multiplexer #(.enable("false")) multiplexer_5 (
    .in0(a[4]), .in1(not_5_out), .out(multiplexer_5_out), .sel(Adder_Subtractor_Select));
  Multiplexer #(.enable("false")) multiplexer_6 (
    .in0(a[5]), .in1(not_6_out), .out(multiplexer_6_out), .sel(Adder_Subtractor_Select));
  Multiplexer #(.enable("false")) multiplexer_7 (
    .in0(a[6]), .in1(not_7_out), .out(multiplexer_7_out), .sel(Adder_Subtractor_Select));
  Multiplexer #(.enable("false")) multiplexer_8 (
    .in0(a[7]), .in1(not_8_out), .out(multiplexer_8_out), .sel(Adder_Subtractor_Select));
  Multiplexer #(.enable("false")) multiplexer_9 (
    .in0(a[8]), .in1(not_9_out), .out(multiplexer_9_out), .sel(Adder_Subtractor_Select));
  Multiplexer #(.enable("false")) multiplexer_10 (
    .in0(a[9]), .in1(not_10_out), .out(multiplexer_10_out), .sel(Adder_Subtractor_Select));
  Multiplexer #(.enable("false")) multiplexer_11 (
    .in0(a[10]), .in1(not_11_out), .out(multiplexer_11_out), .sel(Adder_Subtractor_Select));
  Multiplexer #(.enable("false")) multiplexer_12 (
    .in0(a[11]), .in1(not_12_out), .out(multiplexer_12_out), .sel(Adder_Subtractor_Select));
  Multiplexer #(.enable("false")) multiplexer_13 (
    .in0(a[12]), .in1(not_13_out), .out(multiplexer_13_out), .sel(Adder_Subtractor_Select));
  Multiplexer #(.enable("false")) multiplexer_14 (
    .in0(a[13]), .in1(not_14_out), .out(multiplexer_14_out), .sel(Adder_Subtractor_Select));
  Multiplexer #(.enable("false")) multiplexer_15 (
    .in0(a[14]), .in1(not_15_out), .out(multiplexer_15_out), .sel(Adder_Subtractor_Select));
  Multiplexer #(.enable("false")) multiplexer_16 (
    .in0(a[15]), .in1(not_16_out), .out(multiplexer_16_out), .sel(Adder_Subtractor_Select));
  Adder #(.width(1)) adder_1 (.a(multiplexer_1_out), .b(b[0]), .out(Output[0]), .cin(Carry_in), .cout(adder_1_cout));
  Adder #(.width(1)) adder_2 (
    .a(multiplexer_2_out), .b(b[1]), .out(Output[1]), .cin(adder_1_cout), .cout(adder_2_cout));
  Adder #(.width(1)) adder_3 (
    .a(multiplexer_3_out), .b(b[2]), .out(Output[2]), .cin(adder_2_cout), .cout(adder_3_cout));
  Adder #(.width(1)) adder_4 (
    .a(multiplexer_4_out), .b(b[3]), .out(Output[3]), .cin(adder_3_cout), .cout(adder_4_cout));
  Adder #(.width(1)) adder_5 (
    .a(multiplexer_5_out), .b(b[4]), .out(Output[4]), .cin(adder_4_cout), .cout(adder_5_cout));
  Adder #(.width(1)) adder_6 (
    .a(multiplexer_6_out), .b(b[5]), .out(Output[5]), .cin(adder_5_cout), .cout(adder_6_cout));
  Adder #(.width(1)) adder_7 (
    .a(multiplexer_7_out), .b(b[6]), .out(Output[6]), .cin(adder_6_cout), .cout(adder_7_cout));
  Adder #(.width(1)) adder_8 (
    .a(multiplexer_8_out), .b(b[7]), .out(Output[7]), .cin(adder_7_cout), .cout(adder_8_cout));
  Adder #(.width(1)) adder_9 (
    .a(multiplexer_9_out), .b(b[8]), .out(Output[8]), .cin(adder_8_cout), .cout(adder_9_cout));
  Adder #(.width(1)) adder_10 (
    .a(multiplexer_10_out), .b(b[9]), .out(Output[9]), .cin(adder_9_cout), .cout(adder_10_cout));
  Adder #(.width(1)) adder_11 (
    .a(multiplexer_11_out), .b(b[10]), .out(Output[10]), .cin(adder_10_cout), .cout(adder_11_cout));
  Adder #(.width(1)) adder_12 (
    .a(multiplexer_12_out), .b(b[11]), .out(Output[11]), .cin(adder_11_cout), .cout(adder_12_cout));
  Adder #(.width(1)) adder_13 (
    .a(multiplexer_13_out), .b(b[12]), .out(Output[12]), .cin(adder_12_cout), .cout(adder_13_cout));
  Adder #(.width(1)) adder_14 (
    .a(multiplexer_14_out), .b(b[13]), .out(Output[13]), .cin(adder_13_cout), .cout(adder_14_cout));
  Adder #(.width(1)) adder_15 (
    .a(multiplexer_15_out), .b(b[14]), .out(Output[14]), .cin(adder_14_cout), .cout(adder_15_cout));
  Adder #(.width(1)) adder_16 (
    .a(multiplexer_16_out), .b(b[15]), .out(Output[15]), .cin(adder_15_cout), .cout(Carry_out));
  xor xor_1 (Overflow, adder_15_cout, Carry_out);
endmodule

module INC (
  input  [4:0] flag_in,
  input  [15:0] Data_a,
  input  [15:0] Data_b,
  output [4:0] flag_out,
  output [15:0] Data_d
);

  wire adder_subtractor_1_carry_out, adder_subtractor_1_overflow, flags_in_1_carry_block_in,
       flags_in_1_sign_in, flags_in_1_zero_in;
  wire [4:0] adder_1_out;

  Flags_in flags_in_1 (
    .flag_in(flag_in), .Sign_in(flags_in_1_sign_in), .Zero_in(flags_in_1_zero_in),
    .Carry_block_in(flags_in_1_carry_block_in));  // open: Overflow_in, Carry_in
  Adder #(.width(5)) adder_1 (.a(Data_b[4:0]), .b(5'b00001), .out(adder_1_out), .cin(1'b0));  // open: cout
  Adder_Subtractor adder_subtractor_1 (
    .a({{11{1'b0}}, adder_1_out}), .b(Data_a), .Output(Data_d), .Overflow(adder_subtractor_1_overflow),
    .Adder_Subtractor_Select(1'b0), .Carry_in(1'b0), .Carry_out(adder_subtractor_1_carry_out));
  Flags_out flags_out_1 (
    .Sign_out(flags_in_1_sign_in), .Zero_out(flags_in_1_zero_in), .Overflow_out(adder_subtractor_1_overflow),
    .Carry_out(adder_subtractor_1_carry_out), .Carry_block_out(flags_in_1_carry_block_in), .flag_out(flag_out));
endmodule

module SAVF (
  input  [4:0] flag_in,
  input  [15:0] Data_a,
  input  [15:0] Data_b,
  output [4:0] flag_out,
  output [15:0] Data_d
);

  Flags_in flags_in_1 (
    .flag_in(flag_in), .Sign_in(Data_d[0]), .Zero_in(Data_d[1]), .Overflow_in(Data_d[2]),
    .Carry_in(Data_d[3]), .Carry_block_in(Data_d[4]));
  Flags_out flags_out_1 (.flag_out(flag_out));  // open: Sign_out, Zero_out, Overflow_out, Carry_out, Carry_block_out

  assign Data_d[15:5] = {11{1'b0}};
endmodule

module DEC (
  input  [4:0] flag_in,
  input  [15:0] Data_a,
  input  [15:0] Data_b,
  output [4:0] flag_out,
  output [15:0] Data_d
);

  wire adder_subtractor_1_carry_out, adder_subtractor_1_overflow, flags_in_1_carry_block_in,
       flags_in_1_sign_in, flags_in_1_zero_in;
  wire [4:0] adder_1_out;

  Flags_in flags_in_1 (
    .flag_in(flag_in), .Sign_in(flags_in_1_sign_in), .Zero_in(flags_in_1_zero_in),
    .Carry_block_in(flags_in_1_carry_block_in));  // open: Overflow_in, Carry_in
  Adder #(.width(5)) adder_1 (.a(Data_b[4:0]), .b(5'b00001), .out(adder_1_out), .cin(1'b0));  // open: cout
  Adder_Subtractor adder_subtractor_1 (
    .a({{11{1'b0}}, adder_1_out}), .b(Data_a), .Output(Data_d), .Overflow(adder_subtractor_1_overflow),
    .Adder_Subtractor_Select(1'b1), .Carry_in(1'b1), .Carry_out(adder_subtractor_1_carry_out));
  Flags_out flags_out_1 (
    .Sign_out(flags_in_1_sign_in), .Zero_out(flags_in_1_zero_in), .Overflow_out(adder_subtractor_1_overflow),
    .Carry_out(adder_subtractor_1_carry_out), .Carry_block_out(flags_in_1_carry_block_in), .flag_out(flag_out));
endmodule

// Sign ext
module sign_extension (
  input  in_1,
  input  [7:0] in_2,
  output [15:0] out_3
);

  Multiplexer #(.width(16), .enable("false")) multiplexer_1 (
    .in0({{9{in_2[7]}}, in_2[6:0]}), .in1({in_2, {8{1'b0}}}), .out(out_3), .sel(in_1));
endmodule

module OR (
  input  [4:0] flag_in,
  input  [15:0] Data_a,
  input  [15:0] Data_b,
  output [4:0] flag_out,
  output [15:0] out
);

  wire comparator_1_eq, comparator_1_gt, flags_in_1_carry_block_in, flags_in_1_carry_in,
       flags_in_1_overflow_in;

  Flags_in flags_in_1 (
    .flag_in(flag_in), .Overflow_in(flags_in_1_overflow_in), .Carry_in(flags_in_1_carry_in),
    .Carry_block_in(flags_in_1_carry_block_in));  // open: Sign_in, Zero_in
  assign out = Data_a | Data_b;  // OR_Gate or_1, 16 bits wide
  Comparator #(.width(16)) comparator_1 (
    .a({16{1'b0}}), .b(out), .gt(comparator_1_gt), .eq(comparator_1_eq));  // open: lt
  Flags_out Flags_out (
    .Sign_out(comparator_1_gt), .Zero_out(comparator_1_eq), .Overflow_out(flags_in_1_overflow_in),
    .Carry_out(flags_in_1_carry_in), .Carry_block_out(flags_in_1_carry_block_in), .flag_out(flag_out));
endmodule

module Branch_Unit (
  input  [4:0] flag_in,
  input  [3:0] op,
  output flag_output
);

  wire bc_bcr_1_out_2, bg_bgr_1_out_2, bge_bger_1_out_2, bl_blr_1_out_2, ble_bler_1_out_2, bnc_bncr_1_out_2,
       bns_bnsr_1_out_2, bnv_bnvr_1_out_2, bnz_bnzr_1_out_2, br_brr_1_out_2, bs_bsr_1_out_2,
       bug_bugr_1_out_2, bule_buler_1_out_2, bv_bvr_1_out_2, bz_bzr_1_out_2, unused_1_out_2;

  BR_BRR br_brr_1 (.flag_in(flag_in), .out_2(br_brr_1_out_2));
  unused unused_1 (.flag_in(flag_in), .out_2(unused_1_out_2));
  BL_BLR bl_blr_1 (.flag_in(flag_in), .out_2(bl_blr_1_out_2));
  BGE_BGER bge_bger_1 (.flag_in(flag_in), .out_2(bge_bger_1_out_2));
  BLE_BLER ble_bler_1 (.flag_in(flag_in), .out_2(ble_bler_1_out_2));
  BG_BGR bg_bgr_1 (.flag_in(flag_in), .out_2(bg_bgr_1_out_2));
  BULE_BULER bule_buler_1 (.flag_in(flag_in), .out_2(bule_buler_1_out_2));
  BUG_BUGR bug_bugr_1 (.flag_in(flag_in), .out_2(bug_bugr_1_out_2));
  BZ_BZR bz_bzr_1 (.flag_in(flag_in), .out_2(bz_bzr_1_out_2));
  BNZ_BNZR bnz_bnzr_1 (.flag_in(flag_in), .out_2(bnz_bnzr_1_out_2));
  BC_BCR bc_bcr_1 (.flag_in(flag_in), .out_2(bc_bcr_1_out_2));
  BNC_BNCR bnc_bncr_1 (.flag_in(flag_in), .out_2(bnc_bncr_1_out_2));
  BS_BSR bs_bsr_1 (.flag_in(flag_in), .out_2(bs_bsr_1_out_2));
  BNS_BNSR bns_bnsr_1 (.flag_in(flag_in), .out_2(bns_bnsr_1_out_2));
  BV_BVR bv_bvr_1 (.flag_in(flag_in), .out_2(bv_bvr_1_out_2));
  BNV_BNVR bnv_bnvr_1 (.flag_in(flag_in), .out_2(bnv_bnvr_1_out_2));
  Multiplexer #(.select(4), .enable("false")) multiplexer_1 (
    .in0(br_brr_1_out_2), .in1(unused_1_out_2), .in2(bl_blr_1_out_2), .in3(bge_bger_1_out_2),
    .in4(ble_bler_1_out_2), .in5(bg_bgr_1_out_2), .in6(bule_buler_1_out_2), .in7(bug_bugr_1_out_2),
    .in8(bz_bzr_1_out_2), .in9(bnz_bnzr_1_out_2), .in10(bc_bcr_1_out_2), .in11(bnc_bncr_1_out_2),
    .in12(bs_bsr_1_out_2), .in13(bns_bnsr_1_out_2), .in14(bv_bvr_1_out_2), .in15(bnv_bnvr_1_out_2),
    .out(flag_output), .sel(op));
endmodule

module BL_BLR (
  input  [4:0] flag_in,
  output out_2
);

  xor xor_1 (out_2, flag_in[0], flag_in[2]);
endmodule

module BR_BRR (
  input  [4:0] flag_in,
  output out_2
);


  assign out_2 = 1'b1;
endmodule

// Unused
module unused (
  input  [4:0] flag_in,
  output out_2
);


  assign out_2 = 1'b0;
endmodule

module BGE_BGER (
  input  [4:0] flag_in,
  output out_2
);

  xnor xnor_1 (out_2, flag_in[0], flag_in[2]);
endmodule

module BLE_BLER (
  input  [4:0] flag_in,
  output out_2
);

  wire xor_1_out;

  xor xor_1 (xor_1_out, flag_in[0], flag_in[2]);
  or or_1 (out_2, xor_1_out, flag_in[1]);
endmodule

// BF/BGR
module BG_BGR (
  input  [4:0] flag_in,
  output out_2
);

  wire xor_1_out;

  xor xor_1 (xor_1_out, flag_in[0], flag_in[2]);
  nor nor_1 (out_2, xor_1_out, flag_in[1]);
endmodule

module BULE_BULER (
  input  [4:0] flag_in,
  output out_2
);

  wire not_1_out;

  not not_1 (not_1_out, flag_in[3]);
  or or_1 (out_2, flag_in[1], not_1_out);
endmodule

module BUG_BUGR (
  input  [4:0] flag_in,
  output out_2
);

  wire not_1_out;

  not not_1 (not_1_out, flag_in[3]);
  nor nor_1 (out_2, flag_in[1], not_1_out);
endmodule

module BZ_BZR (
  input  [4:0] flag_in,
  output out_2
);


  assign out_2 = flag_in[1];
endmodule

module BNZ_BNZR (
  input  [4:0] flag_in,
  output out_2
);

  not not_1 (out_2, flag_in[1]);
endmodule

module BC_BCR (
  input  [4:0] flag_in,
  output out_2
);


  assign out_2 = flag_in[3];
endmodule

module BNC_BNCR (
  input  [4:0] flag_in,
  output out_2
);

  not not_1 (out_2, flag_in[3]);
endmodule

module BS_BSR (
  input  [4:0] flag_in,
  output out_2
);


  assign out_2 = flag_in[0];
endmodule

module BNS_BNSR (
  input  [4:0] flag_in,
  output out_2
);

  not not_1 (out_2, flag_in[0]);
endmodule

module BV_BVR (
  input  [4:0] flag_in,
  output out_2
);


  assign out_2 = flag_in[2];
endmodule

module BNV_BNVR (
  input  [4:0] flag_in,
  output out_2
);

  not not_1 (out_2, flag_in[2]);
endmodule

module CLRF (
  input  [4:0] flag_in,
  input  [15:0] Data_a,
  input  [15:0] Data_b,
  output [4:0] flag_out,
  output [15:0] Data_d
);

  Flags_in flags_in_1 (.flag_in(flag_in));  // open: Sign_in, Zero_in, Overflow_in, Carry_in, Carry_block_in
  Flags_out flags_out_1 (
    .Sign_out(1'b0), .Zero_out(1'b0), .Overflow_out(1'b0), .Carry_out(1'b0), .Carry_block_out(1'b0),
    .flag_out(flag_out));

  assign Data_d = {16{1'b0}};
endmodule

module SETHI (
  input  [4:0] flag_in,
  input  [15:0] Data_a,
  input  [15:0] Data_b,
  output [4:0] flag_out,
  output [15:0] Data_d
);

  wire flags_in_1_carry_block_in, flags_in_1_carry_in, flags_in_1_overflow_in, flags_in_1_sign_in,
       flags_in_1_zero_in;

  Flags_in flags_in_1 (
    .flag_in(flag_in), .Sign_in(flags_in_1_sign_in), .Zero_in(flags_in_1_zero_in),
    .Overflow_in(flags_in_1_overflow_in), .Carry_in(flags_in_1_carry_in),
    .Carry_block_in(flags_in_1_carry_block_in));
  Flags_out flags_out_1 (
    .Sign_out(flags_in_1_sign_in), .Zero_out(flags_in_1_zero_in), .Overflow_out(flags_in_1_overflow_in),
    .Carry_out(flags_in_1_carry_in), .Carry_block_out(flags_in_1_carry_block_in), .flag_out(flag_out));

  assign Data_d = {Data_b[7:0], Data_a[7:0]};
endmodule
